// Logisim project 1bswap.circ as structural Verilog: 1 circuit, main circuit swap
module swap (
  input  I1,
  input  I2,
  input  S,
  output O1,
  output O2
);

  wire nand_1_out, nand_2_out, nand_3_out, nand_4_out, nand_5_out, nand_6_out;

  nand nand_1 (nand_1_out, S, S);
  nand nand_2 (nand_2_out, S, S);
  nand nand_3 (nand_3_out, I2, S);
  nand nand_4 (nand_4_out, I1, nand_1_out);
  nand nand_5 (nand_5_out, I2, nand_2_out);
  nand nand_6 (nand_6_out, I1, S);
  nand nand_7 (O1, nand_3_out, nand_4_out);
  nand nand_8 (O2, nand_5_out, nand_6_out);
endmodule
