// Logisim project 2way16bitsMUX.circ as structural Verilog: 1 circuit, main circuit 2way16bitsMUX
module _2way16bitsMUX (
  input  [15:0] in_1,
  input  [15:0] in_2,
  output [15:0] out_3
);

  Multiplexer #(.width(16)) multiplexer_1 (.in0(in_1), .in1(in_2), .out(out_3));  // open: sel, en
endmodule
