// Logisim project 4bit_sort.circ as structural Verilog: 4 circuits, main circuit 1bit_swap
module _1bit_swap (
  input  I1,
  input  I2,
  input  S,
  output O1,
  output O2
);

  wire nand_1_out, nand_2_out, nand_3_out, nand_4_out, nand_5_out, nand_6_out;

  nand nand_1 (nand_1_out, S, S);
  nand nand_2 (nand_2_out, S, S);
  nand nand_3 (nand_3_out, I2, S);
  nand nand_4 (nand_4_out, I1, nand_1_out);
  nand nand_5 (nand_5_out, I2, nand_2_out);
  nand nand_6 (nand_6_out, I1, S);
  nand nand_7 (O1, nand_3_out, nand_4_out);
  nand nand_8 (O2, nand_5_out, nand_6_out);
endmodule

module _4bit_swap (
  input  [3:0] In1,
  input  [3:0] In2,
  input  in_3,
  output [3:0] out1,
  output [3:0] out2
);

  _1bit_swap u_1bit_swap_1 (.I1(In1[0]), .I2(In2[0]), .S(in_3), .O1(out1[0]), .O2(out2[0]));
  _1bit_swap u_1bit_swap_2 (.I1(In1[1]), .I2(In2[1]), .S(in_3), .O1(out1[1]), .O2(out2[1]));
  _1bit_swap u_1bit_swap_3 (.I1(In1[2]), .I2(In2[2]), .S(in_3), .O1(out1[2]), .O2(out2[2]));
  _1bit_swap u_1bit_swap_4 (.I1(In1[3]), .I2(In2[3]), .S(in_3), .O1(out1[3]), .O2(out2[3]));
endmodule

module _4bit_sort (
  input  [3:0] in_1,
  input  [3:0] in_2,
  input  [3:0] in_3,
  input  [3:0] in_4,
  output [3:0] out_5,
  output [3:0] out_6,
  output [3:0] out_7,
  output [3:0] out_8
);

  wire [3:0] if_greater_swap_1_l, if_greater_swap_1_s, if_greater_swap_2_l, if_greater_swap_2_s,
       if_greater_swap_3_s, if_greater_swap_4_l, if_greater_swap_4_s, if_greater_swap_5_s;

  if_greater_swap if_greater_swap_1 (.In1(in_1), .In2(in_2), .s(if_greater_swap_1_s), .l(if_greater_swap_1_l));
  if_greater_swap if_greater_swap_2 (
    .In1(if_greater_swap_1_l), .In2(in_3), .s(if_greater_swap_2_s), .l(if_greater_swap_2_l));
  if_greater_swap if_greater_swap_3 (.In1(if_greater_swap_2_l), .In2(in_4), .s(if_greater_swap_3_s), .l(out_8));
  if_greater_swap if_greater_swap_4 (
    .In1(if_greater_swap_1_s), .In2(if_greater_swap_2_s), .s(if_greater_swap_4_s), .l(if_greater_swap_4_l));
  if_greater_swap if_greater_swap_5 (
    .In1(if_greater_swap_4_l), .In2(if_greater_swap_3_s), .s(if_greater_swap_5_s), .l(out_7));
  if_greater_swap if_greater_swap_6 (.In1(if_greater_swap_4_s), .In2(if_greater_swap_5_s), .s(out_5), .l(out_6));
endmodule

// igsw
module if_greater_swap (
  input  [3:0] In1,
  input  [3:0] In2,
  output [3:0] s,
  output [3:0] l
);

  wire comparator_1_gt;

  Comparator #(.width(4), .mode("unsigned")) comparator_1 (.a(In1), .b(In2), .gt(comparator_1_gt));  // open: eq, lt
  _4bit_swap u_4bit_swap_1 (.In1(In1), .In2(In2), .in_3(comparator_1_gt), .out1(s), .out2(l));
endmodule
