// Logisim project 4bit_sort2.circ as structural Verilog: 3 circuits, main circuit 4bit_swap
module _4bit_swap (
  input  [3:0] In1,
  input  [3:0] In2,
  input  in_3,
  output [3:0] out1,
  output [3:0] out2
);

  _1bit_swap u_1bit_swap_1 (.I1(In1[0]), .I2(In2[0]), .S(in_3), .O1(out1[0]), .O2(out2[0]));
  _1bit_swap u_1bit_swap_2 (.I1(In1[1]), .I2(In2[1]), .S(in_3), .O1(out1[1]), .O2(out2[1]));
  _1bit_swap u_1bit_swap_3 (.I1(In1[2]), .I2(In2[2]), .S(in_3), .O1(out1[2]), .O2(out2[2]));
  _1bit_swap u_1bit_swap_4 (.I1(In1[3]), .I2(In2[3]), .S(in_3), .O1(out1[3]), .O2(out2[3]));
endmodule

module _1bit_swap (
  input  I1,
  input  I2,
  input  S,
  output O1,
  output O2
);

  wire nand_1_out, nand_2_out, nand_3_out, nand_4_out, nand_5_out, nand_6_out;

  nand nand_1 (nand_1_out, S, S);
  nand nand_2 (nand_2_out, S, S);
  nand nand_3 (nand_3_out, I2, S);
  nand nand_4 (nand_4_out, I1, nand_1_out);
  nand nand_5 (nand_5_out, I2, nand_2_out);
  nand nand_6 (nand_6_out, I1, S);
  nand nand_7 (O1, nand_3_out, nand_4_out);
  nand nand_8 (O2, nand_5_out, nand_6_out);
endmodule

module _4bit_sort (
  input  [3:0] A,
  input  [3:0] B,
  input  [3:0] C,
  input  [3:0] D,
  output [3:0] _1,
  output [3:0] _2,
  output [3:0] _3,
  output [3:0] _4
);

  wire comparator_1_gt, comparator_2_gt, comparator_3_gt, comparator_4_gt, comparator_5_gt, comparator_6_gt;
  wire [3:0] n4bit_swap_1_out1, n4bit_swap_1_out2, n4bit_swap_2_out1, n4bit_swap_2_out2, n4bit_swap_3_out1,
       n4bit_swap_4_out1, n4bit_swap_4_out2, n4bit_swap_5_out1;

  Comparator #(.width(4), .mode("unsigned")) comparator_1 (.a(A), .b(B), .gt(comparator_1_gt));  // open: eq, lt
  // Probe on n4bit_swap_1_out1
  _4bit_swap u_4bit_swap_1 (
    .In1(A), .In2(B), .in_3(comparator_1_gt), .out1(n4bit_swap_1_out1), .out2(n4bit_swap_1_out2));
  Comparator #(.width(4), .mode("unsigned")) comparator_2 (
    .a(n4bit_swap_1_out2), .b(C), .gt(comparator_2_gt));  // open: eq, lt
  // Probe on n4bit_swap_2_out2
  // Probe on n4bit_swap_2_out1
  _4bit_swap u_4bit_swap_2 (
    .In1(n4bit_swap_1_out2), .In2(C), .in_3(comparator_2_gt), .out1(n4bit_swap_2_out1),
    .out2(n4bit_swap_2_out2));
  Comparator #(.width(4), .mode("unsigned")) comparator_3 (
    .a(n4bit_swap_2_out2), .b(D), .gt(comparator_3_gt));  // open: eq, lt
  _4bit_swap u_4bit_swap_3 (
    .In1(n4bit_swap_2_out2), .In2(D), .in_3(comparator_3_gt), .out1(n4bit_swap_3_out1), .out2(_4));
  // Probe on _4
  Comparator #(.width(4), .mode("unsigned")) comparator_4 (
    .a(n4bit_swap_1_out1), .b(n4bit_swap_2_out1), .gt(comparator_4_gt));  // open: eq, lt
  _4bit_swap u_4bit_swap_4 (
    .In1(n4bit_swap_1_out1), .In2(n4bit_swap_2_out1), .in_3(comparator_4_gt), .out1(n4bit_swap_4_out1),
    .out2(n4bit_swap_4_out2));
  // Probe on n4bit_swap_4_out2
  Comparator #(.width(4), .mode("unsigned")) comparator_5 (
    .a(n4bit_swap_4_out2), .b(n4bit_swap_3_out1), .gt(comparator_5_gt));  // open: eq, lt
  // Probe on n4bit_swap_5_out1
  _4bit_swap u_4bit_swap_5 (
    .In1(n4bit_swap_4_out2), .In2(n4bit_swap_3_out1), .in_3(comparator_5_gt), .out1(n4bit_swap_5_out1),
    .out2(_3));
  // Probe on _3
  Comparator #(.width(4), .mode("unsigned")) comparator_6 (
    .a(n4bit_swap_4_out1), .b(n4bit_swap_5_out1), .gt(comparator_6_gt));  // open: eq, lt
  _4bit_swap u_4bit_swap_6 (
    .In1(n4bit_swap_4_out1), .In2(n4bit_swap_5_out1), .in_3(comparator_6_gt), .out1(_1), .out2(_2));
endmodule
