// Logisim project CRC_check.circ as structural Verilog: 2 circuits, main circuit main
module main (
  input  [7:0] in_1,
  input  [3:0] in_2
);

  wire button_1_out, clock_1_out, counter_1_carry, counter_2_q, not_1_out;
  wire [2:0] counter_1_q;
  wire [7:0] bit_extender_1_out, multiplexer_1_out, new_minus_1_out_3, register_1_q, shifter_1_out,
       shifter_2_out;

  assign bit_extender_1_out = {{4{1'b0}}, in_2};  // Bit_Extender bit_extender_1
  Shifter shifter_1 (.in(bit_extender_1_out), .\dist (3'b100), .out(shifter_1_out));
  Counter #(.width(3), .max('h5), .ongoal("stay")) counter_1 (
    .Q(counter_1_q), .carry(counter_1_carry), .clk(clock_1_out), .clr(button_1_out));  // open: load, D, count
  Clock clock_1 (.out(clock_1_out));
  Register register_1 (.D(new_minus_1_out_3), .en(not_1_out), .Q(register_1_q), .clk(clock_1_out), .clr(button_1_out));
  not not_1 (not_1_out, counter_1_carry);
  Shifter #(.shift("lr")) shifter_2 (.in(shifter_1_out), .\dist (counter_1_q), .out(shifter_2_out));
  Multiplexer #(.width(8)) multiplexer_1 (
    .in0(in_1), .in1(register_1_q), .out(multiplexer_1_out), .sel(counter_2_q));  // open: en
  Counter #(.width(1), .max('h1), .ongoal("stay")) counter_2 (
    .Q(counter_2_q), .clk(clock_1_out), .clr(button_1_out));  // open: load, D, count, carry
  Button button_1 (.out(button_1_out));
  new_minus new_minus_1 (.in_1(multiplexer_1_out), .in_2(shifter_2_out), .out_3(new_minus_1_out_3));
endmodule

module new_minus (
  input  [7:0] in_1,
  input  [7:0] in_2,
  output [7:0] out_3
);

  wire comparator_1_lt;
  wire [2:0] bitfinder_1_index, bitfinder_2_index;
  wire [7:0] xor_1_out;

  assign xor_1_out = in_1 ^ in_2;  // XOR_Gate xor_1, 8 bits wide
  BitFinder #(.\type ("high1")) bitfinder_1 (.in(in_1), .index(bitfinder_1_index));  // open: found
  BitFinder #(.\type ("high1")) bitfinder_2 (.in(in_2), .index(bitfinder_2_index));  // open: found
  Comparator #(.width(3), .mode("unsigned")) comparator_1 (
    .a(bitfinder_1_index), .b(bitfinder_2_index), .lt(comparator_1_lt));  // open: gt, eq
  Multiplexer #(.width(8)) multiplexer_1 (.in0(xor_1_out), .in1(in_1), .out(out_3), .sel(comparator_1_lt));  // open: en
endmodule
