// Logisim project P0_L0_FSM(1).circ as structural Verilog: 3 circuits, main circuit main
module main (
);

  Register state ();  // open: D, en, Q, clk, clr
endmodule

module fsm (
  input  CLR,
  input  [1:0] in_2,
  output out_3
);

  wire clock_1_out, counter_1_q, register_1_q;
  wire [2:0] change_1_out3, multiplexer_1_out, multiplexer_2_out, state_q;

  Multiplexer #(.width(3), .enable("false")) multiplexer_1 (
    .in0(3'b000), .in1(state_q), .out(multiplexer_1_out), .sel(counter_1_q));
  Clock clock_1 (.out(clock_1_out));
  change change_1 (
    .In1(multiplexer_1_out[2]), .In2(multiplexer_1_out[1]), .In3(multiplexer_1_out[0]), .In4(in_2[1]),
    .In5(in_2[0]), .Out1(change_1_out3[2]), .Out2(change_1_out3[1]), .Out3(change_1_out3[0]));
  Register #(.width(1)) register_1 (.D(CLR), .Q(register_1_q), .clk(clock_1_out), .clr(register_1_q));  // open: en
  Multiplexer #(.width(3), .enable("false")) multiplexer_2 (
    .in0(3'b000), .in1(change_1_out3), .out(multiplexer_2_out), .sel(counter_1_q));
  Counter #(.width(1), .max('h1), .ongoal("stay")) counter_1 (
    .Q(counter_1_q), .clk(clock_1_out));  // open: load, D, count, carry, clr
  Register #(.width(3)) state (.D(multiplexer_2_out), .Q(state_q), .clk(clock_1_out), .clr(register_1_q));  // open: en
  // Probe on state_q
  Comparator #(.width(3), .mode("unsigned")) comparator_1 (.a(state_q), .b(3'b100), .eq(out_3));  // open: gt, lt
endmodule

module change (
  input  In1,
  input  In2,
  input  In3,
  input  In4,
  input  In5,
  output Out1,
  output Out2,
  output Out3
);

  wire and_2_out, and_3_out, and_4_out, and_5_out, and_6_out, and_7_out, and_8_out, not_1_out, not_2_out,
       not_3_out, not_4_out, not_5_out, not_6_out, not_7_out, not_8_out, not_9_out, not_10_out, not_11_out,
       not_12_out, not_13_out, not_14_out, not_15_out, not_16_out, not_17_out, not_18_out, not_19_out,
       not_20_out, not_21_out, not_22_out;

  not not_1 (not_1_out, In1);
  not not_2 (not_2_out, In5);
  not not_3 (not_3_out, In1);
  not not_4 (not_4_out, In2);
  not not_5 (not_5_out, In4);
  not not_6 (not_6_out, In1);
  not not_7 (not_7_out, In2);
  not not_8 (not_8_out, In5);
  not not_9 (not_9_out, In1);
  not not_10 (not_10_out, In3);
  not not_11 (not_11_out, In5);
  not not_12 (not_12_out, In2);
  not not_13 (not_13_out, In3);
  not not_14 (not_14_out, In4);
  not not_15 (not_15_out, In1);
  not not_16 (not_16_out, In2);
  not not_17 (not_17_out, In5);
  not not_18 (not_18_out, In1);
  not not_19 (not_19_out, In3);
  not not_20 (not_20_out, In5);
  not not_21 (not_21_out, In1);
  not not_22 (not_22_out, In4);
  and and_1 (Out1, not_1_out, In2, In3, not_2_out);
  and and_2 (and_2_out, not_3_out, not_4_out, In3, not_5_out);
  and and_3 (and_3_out, not_6_out, not_7_out, In3, not_8_out);
  and and_4 (and_4_out, not_9_out, In2, not_10_out, not_11_out);
  and and_5 (and_5_out, not_12_out, not_13_out, not_14_out, In5);
  and and_6 (and_6_out, not_15_out, not_16_out, In3, not_17_out);
  and and_7 (and_7_out, not_18_out, In2, not_19_out, not_20_out);
  and and_8 (and_8_out, not_21_out, In2, not_22_out, In5);
  or or_1 (Out2, and_2_out, and_3_out, and_4_out);
  or or_2 (Out3, and_5_out, and_6_out, and_7_out, and_8_out);
endmodule
