// Logisim project P0_L0_FSM.circ as structural Verilog: 3 circuits, main circuit fsm
module fsm (
  input  in_1,
  input  [1:0] in_2,
  output out_3
);

  wire clock_1_out;
  wire [2:0] multiplexer_1_out, register_1_q, \状态转移_1_out_3 ;

  Clock clock_1 (.out(clock_1_out));
  \状态转移  \u_状态转移_1  (.in_1(register_1_q), .in_2(in_2), .out_3(\状态转移_1_out_3 ));
  // Probe on register_1_q
  Register #(.width(3)) register_1 (.D(multiplexer_1_out), .Q(register_1_q), .clk(clock_1_out));  // open: en, clr
  Multiplexer #(.width(3)) multiplexer_1 (
    .in0(\状态转移_1_out_3 ), .in1(3'b000), .out(multiplexer_1_out), .sel(in_1));  // open: en
  \output  output_1 (.in_1(\状态转移_1_out_3 ), .x(out_3));
endmodule

module \状态转移  (
  input  [2:0] in_1,
  input  [1:0] in_2,
  output [2:0] out_3
);

  wire and_2_out, and_3_out, and_4_out, and_5_out, and_6_out, and_7_out, and_8_out, and_9_out, not_1_out,
       not_2_out, not_3_out, not_4_out, not_5_out, not_6_out, not_7_out, not_8_out, not_9_out, not_10_out,
       not_11_out, not_12_out, not_13_out, not_14_out, not_15_out, not_16_out, not_17_out;

  not not_1 (not_1_out, in_2[0]);
  not not_2 (not_2_out, in_1[1]);
  not not_3 (not_3_out, in_2[1]);
  not not_4 (not_4_out, in_1[1]);
  not not_5 (not_5_out, in_2[0]);
  not not_6 (not_6_out, in_1[0]);
  not not_7 (not_7_out, in_2[1]);
  not not_8 (not_8_out, in_1[0]);
  not not_9 (not_9_out, in_2[0]);
  not not_10 (not_10_out, in_1[1]);
  not not_11 (not_11_out, in_1[0]);
  not not_12 (not_12_out, in_2[1]);
  not not_13 (not_13_out, in_2[1]);
  and and_1 (out_3[2], in_1[1], in_1[0], not_1_out);
  and and_2 (and_2_out, not_2_out, in_1[0], not_3_out);
  and and_3 (and_3_out, not_4_out, in_1[0], not_5_out);
  and and_4 (and_4_out, in_1[1], not_6_out, not_7_out);
  and and_5 (and_5_out, in_1[1], not_8_out, not_9_out);
  and and_6 (and_6_out, not_10_out, not_11_out, not_12_out, in_2[0]);
  not not_14 (not_14_out, in_1[1]);
  and and_7 (and_7_out, not_14_out, in_1[0], not_15_out);
  not not_15 (not_15_out, in_2[0]);
  and and_8 (and_8_out, in_1[1], not_16_out, not_17_out);
  not not_16 (not_16_out, in_1[0]);
  not not_17 (not_17_out, in_2[0]);
  and and_9 (and_9_out, in_1[1], in_1[0], not_13_out, in_2[0]);
  or or_1 (out_3[1], and_2_out, and_3_out, and_4_out, and_5_out);
  or or_2 (out_3[0], and_6_out, and_7_out, and_8_out, and_9_out);
endmodule

module \output  (
  input  [2:0] in_1,
  output x
);

  wire not_1_out, not_2_out;

  not not_1 (not_1_out, in_1[1]);
  not not_2 (not_2_out, in_1[0]);
  and and_1 (x, in_1[2], not_1_out, not_2_out);
endmodule
