// Logisim project circle_shift.circ as structural Verilog: 2 circuits, main circuit main
module main (
  input  [7:0] in_1,
  input  [2:0] in_2,
  output [7:0] out_3
);

  Multiplexer #(.select(3), .width(8)) multiplexer_1 (
    .in0(in_1), .in1({in_1[6:0], in_1[7]}), .in2({in_1[5:0], in_1[7:6]}), .in3({in_1[4:0], in_1[7:5]}),
    .in4({in_1[3:0], in_1[7:4]}), .in5({in_1[2:0], in_1[7:3]}), .in6({in_1[1:0], in_1[7:2]}),
    .in7({in_1[0], in_1[7:1]}), .out(out_3), .sel(in_2));  // open: en

  // Other names for the same wires on the sheet: _0shift[7:0] = in_1; _1 = in_1[1];
  //   _1shift[7:0] = {in_1[6:0], in_1[7]}; _2shift[7:0] = {in_1[5:0], in_1[7:6]};
  //   _3shift[7:0] = {in_1[4:0], in_1[7:5]}; _4shift[7:0] = {in_1[3:0], in_1[7:4]};
  //   _5shift[7:0] = {in_1[2:0], in_1[7:3]}; _6shift[7:0] = {in_1[1:0], in_1[7:2]};
  //   _7shift[7:0] = {in_1[0], in_1[7:1]}; _2 = in_1[2]; _3 = in_1[3]; _4 = in_1[4]; _5 = in_1[5]; _6 = in_1[6];
  //   _7 = in_1[7]; _0 = in_1[0]
endmodule

module circle_shift (
  input  in_1,
  input  in_2,
  input  in_3,
  input  in_4,
  input  in_5,
  input  in_6,
  input  in_7,
  input  in_8,
  input  in_9,
  input  in_10,
  input  in_11,
  output out_12,
  output out_13,
  output out_14,
  output out_15,
  output out_16,
  output out_17,
  output out_18,
  output out_19
);


  // Notes on the sheet:
  //   out_12: pull=down
  //   out_13: pull=down
  //   out_15: pull=down
  //   out_18: pull=down
  //   out_14: pull=down
  //   out_19: pull=down
  //   out_16: pull=down
  //   out_17: pull=down
endmodule
