// Logisim project crc.circ as structural Verilog: 2 circuits, main circuit main
module main (
  input  [7:0] in_1,
  input  [3:0] in_2,
  output [10:0] out_3
);

  wire [7:0] new_minus_1_out_3, new_minus_2_out_3, new_minus_3_out_3, new_minus_4_out_3, s0, s1, s2, s3, s4;
  wire [7:3] new_minus_5_out_3;

  assign s0 = {{4{1'b0}}, in_2};  // Bit_Extender bit_extender_1
  Shifter shifter_1 (.in(s0), .\dist (3'b001), .out(s1));
  new_minus new_minus_1 (.in_1(in_1), .in_2(s4), .out_3(new_minus_1_out_3));
  Shifter shifter_2 (.in(s1), .\dist (3'b001), .out(s2));
  new_minus new_minus_2 (.in_1(new_minus_3_out_3), .in_2(s2), .out_3(new_minus_2_out_3));
  new_minus new_minus_3 (.in_1(new_minus_1_out_3), .in_2(s3), .out_3(new_minus_3_out_3));
  Shifter shifter_3 (.in(s2), .\dist (3'b001), .out(s3));
  new_minus new_minus_4 (.in_1(new_minus_2_out_3), .in_2(s1), .out_3(new_minus_4_out_3));
  Shifter shifter_4 (.in(s3), .\dist (3'b001), .out(s4));
  new_minus new_minus_5 (.in_1(new_minus_4_out_3), .in_2(s0), .out_3({new_minus_5_out_3, out_3[2:0]}));

  assign out_3[10:3] = in_1;
endmodule

module new_minus (
  input  [7:0] in_1,
  input  [7:0] in_2,
  output [7:0] out_3
);

  wire comparator_1_lt;
  wire [2:0] bitfinder_1_index, bitfinder_2_index;
  wire [7:0] xor_1_out;

  assign xor_1_out = in_1 ^ in_2;  // XOR_Gate xor_1, 8 bits wide
  BitFinder #(.\type ("high1")) bitfinder_1 (.in(in_1), .index(bitfinder_1_index));  // open: found
  BitFinder #(.\type ("high1")) bitfinder_2 (.in(in_2), .index(bitfinder_2_index));  // open: found
  Comparator #(.width(3), .mode("unsigned")) comparator_1 (
    .a(bitfinder_1_index), .b(bitfinder_2_index), .lt(comparator_1_lt));  // open: gt, eq
  Multiplexer #(.width(8)) multiplexer_1 (.in0(xor_1_out), .in1(in_1), .out(out_3), .sel(comparator_1_lt));  // open: en
endmodule
