// Logisim project crc_slidewindow.circ as structural Verilog: 2 circuits, main circuit CRC
module CRC (
  input  [7:0] in_1,
  input  [3:0] in_2,
  output [10:0] out_3
);

  wire [2:0] minus_1_out_3, minus_2_out_3, minus_3_out_3, minus_4_out_3, minus_5_out_3, minus_6_out_3,
       minus_7_out_3;

  minus minus_1 (.in_1(in_1[7:4]), .in_2(in_2), .out_3(minus_1_out_3));  // open: out_4
  minus minus_2 (.in_1({minus_1_out_3, in_1[3]}), .in_2(in_2), .out_3(minus_2_out_3));  // open: out_4
  minus minus_3 (.in_1({minus_2_out_3, in_1[2]}), .in_2(in_2), .out_3(minus_3_out_3));  // open: out_4
  minus minus_4 (.in_1({minus_3_out_3, in_1[1]}), .in_2(in_2), .out_3(minus_4_out_3));  // open: out_4
  minus minus_5 (.in_1({minus_4_out_3, in_1[0]}), .in_2(in_2), .out_3(minus_5_out_3));  // open: out_4
  minus minus_6 (.in_1({minus_5_out_3, 1'b0}), .in_2(in_2), .out_3(minus_6_out_3));  // open: out_4
  minus minus_7 (.in_1({minus_6_out_3, 1'b0}), .in_2(in_2), .out_3(minus_7_out_3));  // open: out_4
  minus minus_8 (.in_1({minus_7_out_3, 1'b0}), .in_2(in_2), .out_3(out_3[2:0]));  // open: out_4

  assign out_3[10:3] = in_1;
endmodule

module minus (
  input  [3:0] in_1,
  input  [3:0] in_2,
  output [2:0] out_3,
  output out_4
);

  wire [3:0] xor_1_out;
  wire [3:3] multiplexer_1_out;

  assign xor_1_out = in_1 ^ in_2;  // XOR_Gate xor_1, 4 bits wide
  Multiplexer #(.width(4)) multiplexer_1 (
    .in0(in_1), .in1(xor_1_out), .out({multiplexer_1_out[3], out_3}), .sel(in_1[3]));  // open: en

  assign out_4 = in_1[3];
endmodule
