// Logisim project fiber.circ as structural Verilog: 2 circuits, main circuit main
module main (
  input  [2:0] in_1,
  output [3:0] out_2
);

  wire button_1_out, clock_1_out, comparator_1_eq;
  wire [3:0] bit_extender_1_out, counter_1_q;

  Button button_1 (.out(button_1_out));
  Counter #(.width(4), .max('hf)) counter_1 (
    .count(1'b1), .Q(counter_1_q), .clk(clock_1_out), .clr(button_1_out));  // open: load, D, carry
  Clock clock_1 (.out(clock_1_out));
  cal cal_1 (.in_1(button_1_out), .in_2(comparator_1_eq), .out_3(out_2));
  assign bit_extender_1_out = {{1{1'b0}}, in_1};  // Bit_Extender bit_extender_1
  Comparator #(.width(4)) comparator_1 (.a(bit_extender_1_out), .b(counter_1_q), .eq(comparator_1_eq));  // open: gt, lt
endmodule

module cal (
  input  in_1,
  input  in_2,
  output [3:0] out_3
);

  wire clock_1_out, counter_1_q;
  wire [3:0] adder_1_out, multiplexer_1_out, new_q, prev_q;

  Counter #(.width(1), .max('h1), .ongoal("stay")) counter_1 (
    .Q(counter_1_q), .clk(clock_1_out), .clr(in_1));  // open: load, D, count, carry
  Clock clock_1 (.out(clock_1_out));
  Multiplexer #(.width(4)) multiplexer_1 (
    .in0(4'b0001), .in1(adder_1_out), .out(multiplexer_1_out), .sel(counter_1_q));  // open: en
  Register #(.width(4)) prev (.D(new_q), .Q(prev_q), .clk(clock_1_out), .clr(in_1));  // open: en
  Register #(.width(4)) \new  (.D(multiplexer_1_out), .Q(new_q), .clk(clock_1_out), .clr(in_1));  // open: en
  Adder #(.width(4)) adder_1 (.a(prev_q), .b(new_q), .out(adder_1_out));  // open: cin, cout
  Register #(.width(4)) register_1 (.D(new_q), .en(clock_1_out), .Q(out_3), .clk(in_2));  // open: clr
endmodule
