// Logisim project fiber_pro.circ as structural Verilog: 5 circuits, main circuit main
module main (
  input  [31:0] in_1,
  output [31:0] out_2
);

  wire ans____a, button_1_out, clock_1_out, comparator_1_eq, comparator_1_lt, counter_1_q, isend, not_1_out,
       or_1_out;
  wire [31:0] a_out_7, a_out_8, a_out_9, a_out_10, ans_out_7, ans_out_8, ans_out_9, ans_out_10,
       mat_mult_s_1_out_7, mat_mult_s_1_out_8, mat_selfmult_1_out_6, mat_selfmult_1_out_7,
       mat_selfmult_1_out_8, mat_selfmult_1_out_9, multiplexer_1_out, multiplexer_2_out, multiplexer_3_out,
       multiplexer_4_out, multiplexer_5_out, multiplexer_6_out, multiplexer_7_out, multiplexer_8_out,
       multiplexer_9_out, res00, res01, res10, res11, shifter_1_out;
  wire [31:1] y_q;

  Counter #(.width(1), .max('h1), .ongoal("stay")) counter_1 (
    .Q(counter_1_q), .clk(clock_1_out), .clr(button_1_out));  // open: load, D, count, carry
  Clock clock_1 (.out(clock_1_out));
  Button button_1 (.out(button_1_out));
  Multiplexer #(.width(32)) multiplexer_1 (
    .in0(in_1), .in1(shifter_1_out), .out(multiplexer_1_out), .sel(counter_1_q));  // open: en
  Register #(.width(32)) y (
    .D(multiplexer_1_out), .Q({y_q, ans____a}), .clk(clock_1_out), .clr(button_1_out));  // open: en
  Comparator #(.width(32), .mode("unsigned")) comparator_1 (
    .a({y_q, ans____a}), .b({32{1'b0}}), .eq(comparator_1_eq), .lt(comparator_1_lt));  // open: gt
  Shifter #(.width(32), .shift("lr")) shifter_1 (.in({y_q, ans____a}), .\dist (5'b00001), .out(shifter_1_out));
  or or_1 (or_1_out, comparator_1_eq, comparator_1_lt);
  and and_1 (isend, or_1_out, or_1_out, counter_1_q);
  Multiplexer #(.width(32)) multiplexer_2 (
    .in0(32'h1), .in1(mat_selfmult_1_out_6), .out(multiplexer_2_out), .sel(counter_1_q));  // open: en
  Multiplexer #(.width(32)) multiplexer_3 (
    .in0(32'h1), .in1(mat_selfmult_1_out_7), .out(multiplexer_3_out), .sel(counter_1_q));  // open: en
  Multiplexer #(.width(32)) multiplexer_4 (
    .in0(32'h1), .in1(mat_selfmult_1_out_8), .out(multiplexer_4_out), .sel(counter_1_q));  // open: en
  Multiplexer #(.width(32)) multiplexer_5 (
    .in0({32{1'b0}}), .in1(mat_selfmult_1_out_9), .out(multiplexer_5_out), .sel(counter_1_q));  // open: en
  Multiplexer #(.width(32)) multiplexer_6 (
    .in0(32'h1), .in1(res00), .out(multiplexer_6_out), .sel(counter_1_q));  // open: en
  Multiplexer #(.width(32)) multiplexer_7 (
    .in0({32{1'b0}}), .in1(res01), .out(multiplexer_7_out), .sel(counter_1_q));  // open: en
  Multiplexer #(.width(32)) multiplexer_8 (
    .in0({32{1'b0}}), .in1(res10), .out(multiplexer_8_out), .sel(counter_1_q));  // open: en
  Multiplexer #(.width(32)) multiplexer_9 (
    .in0(32'h1), .in1(res11), .out(multiplexer_9_out), .sel(counter_1_q));  // open: en
  store_mat a (
    .in_1(multiplexer_2_out), .in_2(multiplexer_3_out), .in_3(multiplexer_4_out), .in_4(multiplexer_5_out),
    .out_7(a_out_7), .out_8(a_out_8), .out_9(a_out_9), .out_10(a_out_10), .in_5(button_1_out),
    .in_6(not_1_out));
  store_mat ans (
    .in_1(multiplexer_6_out), .in_2(multiplexer_7_out), .in_3(multiplexer_8_out), .in_4(multiplexer_9_out),
    .out_7(ans_out_7), .out_8(ans_out_8), .out_9(ans_out_9), .out_10(ans_out_10), .in_5(button_1_out),
    .in_6(not_1_out));
  mat_selfmult mat_selfmult_1 (
    .in_1(a_out_7), .in_2(a_out_8), .in_3(a_out_9), .in_5(a_out_10), .out_6(mat_selfmult_1_out_6),
    .out_7(mat_selfmult_1_out_7), .out_8(mat_selfmult_1_out_8), .out_9(mat_selfmult_1_out_9), .in_4(not_1_out));
  mat_mult_s mat_mult_s_1 (
    .in_1(ans_out_7), .in_2(32'h1), .in_3(ans_out_8), .in_4(ans_out_9), .in_5({32{1'b0}}), .in_6(ans_out_10),
    .out_7(mat_mult_s_1_out_7), .out_8(mat_mult_s_1_out_8));
  not not_1 (not_1_out, isend);
  mat_multt mat_multt_1 (
    .in_2(a_out_7), .in_3(ans_out_7), .in_4(a_out_8), .in_5(ans_out_8), .in_6(a_out_9), .in_7(ans_out_9),
    .in_8(a_out_10), .in_9(ans_out_10), .out_10(res00), .out_11(res01), .out_12(res10), .out_13(res11),
    .en(ans____a));
  Register #(.width(32)) register_1 (
    .D(mat_mult_s_1_out_7), .en(isend), .clk(clock_1_out), .clr(button_1_out));  // open: Q
  Register #(.width(32)) register_2 (
    .D(mat_mult_s_1_out_8), .en(isend), .Q(out_2), .clk(clock_1_out), .clr(button_1_out));

  // Notes on the sheet:
  //   this is where control signal gives out
  //   this is where a self_mult
  //   this is where ans update 
endmodule

module store_mat (
  input  [31:0] in_1,
  input  [31:0] in_2,
  input  [31:0] in_3,
  input  [31:0] in_4,
  input  in_5,
  input  in_6,
  output [31:0] out_7,
  output [31:0] out_8,
  output [31:0] out_9,
  output [31:0] out_10
);

  wire clock_1_out;

  Register #(.width(32)) register_1 (.D(in_1), .en(in_6), .Q(out_7), .clk(clock_1_out), .clr(in_5));
  Register #(.width(32)) register_2 (.D(in_2), .Q(out_8), .clk(clock_1_out), .clr(in_5));  // open: en
  Register #(.width(32)) register_3 (.D(in_3), .Q(out_9), .clk(clock_1_out), .clr(in_5));  // open: en
  Register #(.width(32)) register_4 (.D(in_4), .Q(out_10), .clk(clock_1_out), .clr(in_5));  // open: en
  Clock clock_1 (.out(clock_1_out));

  // Notes on the sheet:
  //   a00
  //   a01
  //   a10
  //   a11
endmodule

module mat_selfmult (
  input  [31:0] in_1,
  input  [31:0] in_2,
  input  [31:0] in_3,
  input  in_4,
  input  [31:0] in_5,
  output [31:0] out_6,
  output [31:0] out_7,
  output [31:0] out_8,
  output [31:0] out_9
);

  mat_multt mat_multt_1 (
    .in_2(in_1), .in_3(in_1), .in_4(in_2), .in_5(in_2), .in_6(in_3), .in_7(in_3), .in_8(in_5), .in_9(in_5),
    .out_10(out_6), .out_11(out_7), .out_12(out_8), .out_13(out_9), .en(in_4));

  // Notes on the sheet:
  //   a00
  //   a01
  //   a10
  //   a11
endmodule

module mat_multt (
  input  en,
  input  [31:0] in_2,
  input  [31:0] in_3,
  input  [31:0] in_4,
  input  [31:0] in_5,
  input  [31:0] in_6,
  input  [31:0] in_7,
  input  [31:0] in_8,
  input  [31:0] in_9,
  output [31:0] out_10,
  output [31:0] out_11,
  output [31:0] out_12,
  output [31:0] out_13
);

  wire not_1_out;
  wire [31:0] adder_1_out, adder_2_out, adder_3_out, adder_4_out, multiplier_1_out, multiplier_2_out,
       multiplier_3_out, multiplier_4_out, multiplier_5_out, multiplier_6_out, multiplier_7_out,
       multiplier_8_out;

  Multiplier #(.width(32)) multiplier_1 (.a(in_2), .b(in_3), .out(multiplier_1_out));  // open: cin, cout
  Multiplier #(.width(32)) multiplier_2 (.a(in_4), .b(in_7), .out(multiplier_2_out));  // open: cin, cout
  Multiplier #(.width(32)) multiplier_3 (.a(in_2), .b(in_5), .out(multiplier_3_out));  // open: cin, cout
  Multiplier #(.width(32)) multiplier_4 (.a(in_4), .b(in_9), .out(multiplier_4_out));  // open: cin, cout
  Multiplier #(.width(32)) multiplier_5 (.a(in_6), .b(in_3), .out(multiplier_5_out));  // open: cin, cout
  Multiplier #(.width(32)) multiplier_6 (.a(in_8), .b(in_7), .out(multiplier_6_out));  // open: cin, cout
  Multiplier #(.width(32)) multiplier_7 (.a(in_6), .b(in_5), .out(multiplier_7_out));  // open: cin, cout
  Multiplier #(.width(32)) multiplier_8 (.a(in_8), .b(in_9), .out(multiplier_8_out));  // open: cin, cout
  not not_1 (not_1_out, en);
  Adder #(.width(32)) adder_1 (.a(multiplier_1_out), .b(multiplier_2_out), .out(adder_1_out));  // open: cin, cout
  Adder #(.width(32)) adder_2 (.a(multiplier_3_out), .b(multiplier_4_out), .out(adder_2_out));  // open: cin, cout
  Adder #(.width(32)) adder_3 (.a(multiplier_5_out), .b(multiplier_6_out), .out(adder_3_out));  // open: cin, cout
  Adder #(.width(32)) adder_4 (.a(multiplier_7_out), .b(multiplier_8_out), .out(adder_4_out));  // open: cin, cout
  Multiplexer #(.width(32)) multiplexer_1 (.in0(adder_1_out), .in1(in_3), .out(out_10), .sel(not_1_out));  // open: en
  Multiplexer #(.width(32)) multiplexer_2 (.in0(adder_2_out), .in1(in_5), .out(out_11), .sel(not_1_out));  // open: en
  Multiplexer #(.width(32)) multiplexer_3 (.in0(adder_3_out), .in1(in_7), .out(out_12), .sel(not_1_out));  // open: en
  Multiplexer #(.width(32)) multiplexer_4 (.in0(adder_4_out), .in1(in_9), .out(out_13), .sel(not_1_out));  // open: en

  // Other names for the same wires on the sheet: a00[31:0] = in_2; a01[31:0] = in_4; a10[31:0] = in_6;
  //   a11[31:0] = in_8; b00[31:0] = in_3; b01[31:0] = in_5; b10[31:0] = in_7; b11[31:0] = in_9

  // Notes on the sheet:
  //   a00
  //   a01
  //   a10
  //   a11
  //   b00
  //   b01
  //   b10
  //   b11
endmodule

module mat_mult_s (
  input  [31:0] in_1,
  input  [31:0] in_2,
  input  [31:0] in_3,
  input  [31:0] in_4,
  input  [31:0] in_5,
  input  [31:0] in_6,
  output [31:0] out_7,
  output [31:0] out_8
);

  wire [31:0] multiplier_1_out, multiplier_2_out, multiplier_3_out, multiplier_4_out;

  Multiplier #(.width(32)) multiplier_1 (.a(in_1), .b(in_2), .out(multiplier_1_out));  // open: cin, cout
  Multiplier #(.width(32)) multiplier_2 (.a(in_3), .b(in_5), .out(multiplier_2_out));  // open: cin, cout
  Multiplier #(.width(32)) multiplier_3 (.a(in_4), .b(in_2), .out(multiplier_3_out));  // open: cin, cout
  Multiplier #(.width(32)) multiplier_4 (.a(in_6), .b(in_5), .out(multiplier_4_out));  // open: cin, cout
  Adder #(.width(32)) adder_1 (.a(multiplier_1_out), .b(multiplier_2_out), .out(out_7));  // open: cin, cout
  Adder #(.width(32)) adder_2 (.a(multiplier_3_out), .b(multiplier_4_out), .out(out_8));  // open: cin, cout

  // Other names for the same wires on the sheet: a00[31:0] = in_1; a01[31:0] = in_3; a10[31:0] = in_4;
  //   a11[31:0] = in_6; b00[31:0] = in_2; b10[31:0] = in_5

  // Notes on the sheet:
  //   a00
  //   a01
  //   a10
  //   a11
  //   b00
  //   b10
endmodule
