// Logisim project fsm.circ as structural Verilog: 9 circuits, main circuit fsm
module fsm (
  input  in_1,
  input  [1:0] in_2,
  output out_3
);

  wire clock_1_out, m0_1_o, m1_1_o, m2_1_o, m3_1_o;
  wire [2:0] multiplexer_1_out, multiplexer_2_out, multiplexer_3_out, multiplexer_4_out, n0, n1, n2, n3, s0,
       s1, s2, s3;

  Register #(.width(3)) register_1 (.D(multiplexer_1_out), .Q(s0), .clk(clock_1_out));  // open: en, clr
  Multiplexer #(.width(3)) multiplexer_1 (.in0(n0), .in1(3'b000), .out(multiplexer_1_out), .sel(in_1));  // open: en
  Register #(.width(3)) register_2 (.D(multiplexer_2_out), .Q(s1), .clk(clock_1_out));  // open: en, clr
  Multiplexer #(.width(3)) multiplexer_2 (.in0(n1), .in1(3'b000), .out(multiplexer_2_out), .sel(in_1));  // open: en
  Register #(.width(3)) register_3 (.D(multiplexer_3_out), .Q(s2), .clk(clock_1_out));  // open: en, clr
  Multiplexer #(.width(3)) multiplexer_3 (.in0(n2), .in1(3'b000), .out(multiplexer_3_out), .sel(in_1));  // open: en
  Register #(.width(3)) register_4 (.D(multiplexer_4_out), .Q(s3), .clk(clock_1_out));  // open: en, clr
  Multiplexer #(.width(3)) multiplexer_4 (.in0(n3), .in1(3'b000), .out(multiplexer_4_out), .sel(in_1));  // open: en
  Clock clock_1 (.out(clock_1_out));
  st_trans0 st_trans0_1 (
    .s2(s0[2]), .s1(s0[1]), .s0(s0[0]), .in1(in_2[1]), .in0(in_2[0]), .n2(n0[2]), .n1(n0[1]), .n0(n0[0]));
  st_trans1 st_trans1_1 (
    .s2(s1[2]), .s1(s1[1]), .s0(s1[0]), .in1(in_2[1]), .in0(in_2[0]), .n2(n1[2]), .n1(n1[1]), .n0(n1[0]));
  st_trans2 st_trans2_1 (
    .s2(s2[2]), .s1(s2[1]), .s0(s2[0]), .in1(in_2[1]), .in0(in_2[0]), .n2(n2[2]), .n1(n2[1]), .n0(n2[0]));
  st_trans3 st_trans3_1 (
    .s2(s3[2]), .n2(n3[2]), .s1(s3[1]), .s0(s3[0]), .in1(in_2[1]), .n1(n3[1]), .in0(in_2[0]), .n0(n3[0]));
  m0 m0_1 (.s2(s0[2]), .s1(s0[1]), .s0(s0[0]), .in1(in_2[1]), .in0(in_2[0]), .o(m0_1_o));
  m1 m1_1 (.s2(s1[2]), .s1(s1[1]), .s0(s1[0]), .in1(in_2[1]), .in0(in_2[0]), .o(m1_1_o));
  m2 m2_1 (.s2(s2[2]), .s1(s2[1]), .s0(s2[0]), .in1(in_2[1]), .in0(in_2[0]), .o(m2_1_o));
  m3 m3_1 (.s2(s3[2]), .s1(s3[1]), .s0(s3[0]), .in1(in_2[1]), .in0(in_2[0]), .o(m3_1_o));
  or or_1 (out_3, m0_1_o, m1_1_o, m2_1_o, m3_1_o);

  // Other names for the same wires on the sheet: in0 = in_2[0]; in1 = in_2[1]
endmodule

module st_trans0 (
  input  s2,
  input  s1,
  input  s0,
  input  in1,
  input  in0,
  output n2,
  output n1,
  output n0
);

  wire and_2_out, and_3_out, and_4_out, and_5_out, and_6_out, and_7_out, and_8_out, not_1_out, not_2_out,
       not_3_out, not_4_out, not_5_out, not_6_out, not_7_out, not_8_out, not_9_out, not_10_out, not_11_out,
       not_12_out, not_13_out, not_14_out, not_15_out, not_16_out, not_17_out, not_18_out, not_19_out,
       not_20_out, not_21_out;

  not not_1 (not_1_out, s2);
  not not_2 (not_2_out, in0);
  not not_3 (not_3_out, s2);
  not not_4 (not_4_out, s1);
  not not_5 (not_5_out, in1);
  not not_6 (not_6_out, s2);
  not not_7 (not_7_out, s0);
  not not_8 (not_8_out, in1);
  not not_9 (not_9_out, s1);
  not not_10 (not_10_out, s0);
  not not_11 (not_11_out, in1);
  not not_12 (not_12_out, s2);
  not not_13 (not_13_out, s0);
  not not_14 (not_14_out, in1);
  not not_15 (not_15_out, in0);
  not not_16 (not_16_out, s2);
  not not_17 (not_17_out, in1);
  not not_18 (not_18_out, s2);
  not not_19 (not_19_out, in0);
  not not_20 (not_20_out, s1);
  not not_21 (not_21_out, in1);
  and and_1 (n2, not_1_out, s1, s0, not_2_out);
  and and_2 (and_2_out, not_3_out, not_4_out, s0, not_5_out, in0);
  and and_3 (and_3_out, not_6_out, s1, not_7_out, not_8_out);
  and and_4 (and_4_out, not_9_out, not_10_out, not_11_out, in0);
  and and_5 (and_5_out, not_12_out, s1, not_13_out, not_14_out, not_15_out);
  and and_6 (and_6_out, not_16_out, s1, s0, not_17_out, in0);
  and and_7 (and_7_out, not_18_out, s1, s0, in1, not_19_out);
  and and_8 (and_8_out, s2, not_20_out, not_21_out, in0);
  or or_1 (n1, and_2_out, and_3_out);
  or or_2 (n0, and_4_out, and_5_out, and_6_out, and_7_out, and_8_out);
endmodule

module st_trans1 (
  input  s2,
  input  s1,
  input  s0,
  input  in1,
  input  in0,
  output n2,
  output n1,
  output n0
);

  wire and_2_out, and_3_out, and_4_out, and_5_out, and_6_out, and_7_out, and_8_out, not_1_out, not_2_out,
       not_3_out, not_4_out, not_5_out, not_6_out, not_7_out, not_8_out, not_9_out, not_10_out, not_11_out,
       not_12_out, not_13_out, not_14_out, not_15_out, not_16_out, not_17_out, not_18_out, not_19_out,
       not_20_out;

  not not_1 (not_1_out, s2);
  not not_2 (not_2_out, in0);
  not not_3 (not_3_out, s2);
  not not_4 (not_4_out, s1);
  not not_5 (not_5_out, in1);
  not not_6 (not_6_out, s2);
  not not_7 (not_7_out, s0);
  not not_8 (not_8_out, in1);
  not not_9 (not_9_out, s2);
  not not_10 (not_10_out, s0);
  not not_11 (not_11_out, in0);
  not not_12 (not_12_out, s1);
  not not_13 (not_13_out, s0);
  not not_14 (not_14_out, in1);
  not not_15 (not_15_out, s2);
  not not_16 (not_16_out, in0);
  not not_17 (not_17_out, s2);
  not not_18 (not_18_out, in1);
  not not_19 (not_19_out, s1);
  not not_20 (not_20_out, in1);
  and and_1 (n2, not_1_out, s1, s0, not_2_out);
  and and_2 (and_2_out, not_3_out, not_4_out, s0, not_5_out, in0);
  and and_3 (and_3_out, not_6_out, s1, not_7_out, not_8_out, in0);
  and and_4 (and_4_out, not_9_out, s1, not_10_out, in1, not_11_out);
  and and_5 (and_5_out, not_12_out, not_13_out, not_14_out, in0);
  and and_6 (and_6_out, not_15_out, s1, in1, not_16_out);
  and and_7 (and_7_out, not_17_out, s1, s0, not_18_out, in0);
  and and_8 (and_8_out, s2, not_19_out, not_20_out, in0);
  or or_1 (n1, and_2_out, and_3_out, and_4_out);
  or or_2 (n0, and_5_out, and_6_out, and_7_out, and_8_out);
endmodule

module st_trans2 (
  input  s2,
  input  s1,
  input  s0,
  input  in1,
  input  in0,
  output n2,
  output n1,
  output n0
);

  wire and_2_out, and_3_out, and_4_out, and_5_out, and_6_out, not_1_out, not_2_out, not_3_out, not_4_out,
       not_5_out, not_6_out, not_7_out, not_8_out, not_9_out, not_10_out, not_11_out, not_12_out, not_13_out,
       not_14_out, not_15_out, not_16_out, not_17_out, not_18_out, not_19_out;

  not not_1 (not_1_out, s2);
  not not_2 (not_2_out, s0);
  not not_3 (not_3_out, in0);
  not not_4 (not_4_out, s2);
  not not_5 (not_5_out, s1);
  not not_6 (not_6_out, in1);
  not not_7 (not_7_out, in0);
  not not_8 (not_8_out, s2);
  not not_9 (not_9_out, s0);
  not not_10 (not_10_out, in1);
  not not_11 (not_11_out, in0);
  not not_12 (not_12_out, s2);
  not not_13 (not_13_out, in1);
  not not_14 (not_14_out, s1);
  not not_15 (not_15_out, s0);
  not not_16 (not_16_out, in1);
  not not_17 (not_17_out, s2);
  not not_18 (not_18_out, s0);
  not not_19 (not_19_out, in1);
  and and_1 (n2, not_1_out, s1, not_2_out, in1, not_3_out);
  and and_2 (and_2_out, not_4_out, not_5_out, s0, not_6_out, not_7_out);
  and and_3 (and_3_out, not_8_out, s1, not_9_out, not_10_out, not_11_out);
  and and_4 (and_4_out, not_12_out, not_13_out, in0);
  and and_5 (and_5_out, not_14_out, not_15_out, not_16_out, in0);
  and and_6 (and_6_out, not_17_out, s1, not_18_out, not_19_out);
  or or_1 (n1, and_2_out, and_3_out);
  or or_2 (n0, and_4_out, and_5_out, and_6_out);
endmodule

module st_trans3 (
  input  s2,
  input  s1,
  input  s0,
  input  in1,
  input  in0,
  output n2,
  output n1,
  output n0
);

  wire and_2_out, and_3_out, and_4_out, and_5_out, and_6_out, not_1_out, not_2_out, not_3_out, not_4_out,
       not_5_out, not_6_out, not_7_out, not_8_out, not_9_out, not_10_out, not_11_out, not_12_out, not_13_out,
       not_14_out, not_15_out, not_16_out, not_17_out, not_18_out;

  not not_1 (not_1_out, s2);
  not not_2 (not_2_out, s0);
  not not_3 (not_3_out, in0);
  not not_4 (not_4_out, s2);
  not not_5 (not_5_out, s1);
  not not_6 (not_6_out, in0);
  not not_7 (not_7_out, s2);
  not not_8 (not_8_out, s0);
  not not_9 (not_9_out, in1);
  not not_10 (not_10_out, in0);
  not not_11 (not_11_out, s2);
  not not_12 (not_12_out, in1);
  not not_13 (not_13_out, s1);
  not not_14 (not_14_out, s0);
  not not_15 (not_15_out, in1);
  not not_16 (not_16_out, s2);
  not not_17 (not_17_out, s0);
  not not_18 (not_18_out, in1);
  and and_1 (n2, not_1_out, s1, not_2_out, in1, not_3_out);
  and and_2 (and_2_out, not_4_out, not_5_out, s0, in1, not_6_out);
  and and_3 (and_3_out, not_7_out, s1, not_8_out, not_9_out, not_10_out);
  and and_4 (and_4_out, not_11_out, not_12_out, in0);
  and and_5 (and_5_out, not_13_out, not_14_out, not_15_out, in0);
  and and_6 (and_6_out, not_16_out, s1, not_17_out, not_18_out);
  or or_1 (n1, and_2_out, and_3_out);
  or or_2 (n0, and_4_out, and_5_out, and_6_out);
endmodule

module m0 (
  input  s2,
  input  s1,
  input  s0,
  input  in1,
  input  in0,
  output o
);

  wire not_1_out, not_2_out;

  not not_1 (not_1_out, s2);
  not not_2 (not_2_out, in0);
  and and_1 (o, not_1_out, s1, s0, not_2_out);
endmodule

module m1 (
  input  s2,
  input  s1,
  input  s0,
  input  in1,
  input  in0,
  output o
);

  wire not_1_out, not_2_out;

  not not_1 (not_1_out, s2);
  not not_2 (not_2_out, in0);
  and and_1 (o, not_1_out, s1, s0, not_2_out);
endmodule

module m2 (
  input  s2,
  input  s1,
  input  s0,
  input  in1,
  input  in0,
  output o
);

  wire not_1_out, not_2_out, not_3_out;

  not not_1 (not_1_out, s2);
  not not_2 (not_2_out, s0);
  not not_3 (not_3_out, in0);
  and and_1 (o, not_1_out, s1, not_2_out, not_3_out);
endmodule

module m3 (
  input  s2,
  input  s1,
  input  s0,
  input  in1,
  input  in0,
  output o
);

  wire not_1_out, not_2_out, not_3_out;

  not not_1 (not_1_out, s2);
  not not_2 (not_2_out, s0);
  not not_3 (not_3_out, in0);
  and and_1 (o, not_1_out, s1, not_2_out, not_3_out);
endmodule
