// Logisim project ftoi.circ as structural Verilog: 2 circuits, main circuit ftoi
module ftoi (
  input  [15:0] in_1,
  output [31:0] out_2
);

  wire isdeno, isinf_or_nan;
  wire [31:0] multiplexer_1_out, nor_num;

  Comparator #(.width(5)) comparator_1 (.a(in_1[14:10]), .b({5{1'b1}}), .eq(isinf_or_nan));  // open: gt, lt
  cal cal_1 (.in_1(in_1[15]), .in_2(in_1[14:10]), .in_3(in_1[9:0]), .out_4(nor_num));
  Comparator #(.width(5)) comparator_2 (.a(in_1[14:10]), .b({5{1'b0}}), .eq(isdeno));  // open: gt, lt
  Multiplexer #(.width(32)) multiplexer_1 (
    .in0(nor_num), .in1({32{1'b0}}), .out(multiplexer_1_out), .sel(isdeno));  // open: en
  Multiplexer #(.width(32)) multiplexer_2 (
    .in0(multiplexer_1_out), .in1({32{1'b0}}), .out(out_2), .sel(isinf_or_nan));  // open: en

  // Other names for the same wires on the sheet: frac[9:0] = in_1[9:0]; expo[4:0] = in_1[14:10]; sign = in_1[15]
endmodule

module cal (
  input  in_1,
  input  [4:0] in_2,
  input  [9:0] in_3,
  output [31:0] out_4
);

  wire _2, e0, e1, e2, e3, e4;
  wire [4:0] subtractor_1_out;
  wire [31:0] _2_frac, _2_frac__1, _2_frac__2, _2_frac__3, _2_frac__4, _2_frac__5, _2_frac__6, _2_frac__7,
       _2_frac__8, _2_frac__9, _2_frac__10, adder_1_out, adder_2_out, adder_3_out, adder_4_out, adder_5_out,
       adder_6_out, adder_7_out, adder_8_out, adder_9_out, adder_10_out, multiplexer_12_out,
       multiplexer_13_out, multiplexer_14_out, multiplexer_15_out, multiplexer_16_out, multiplexer_17_out,
       multiplier_1_out, multiplier_2_out, multiplier_3_out, negator_1_out, shifter_1_out, shifter_2_out,
       shifter_3_out, shifter_4_out, shifter_5_out, shifter_6_out, shifter_7_out, shifter_8_out,
       shifter_9_out, shifter_10_out;

  Subtractor #(.width(5)) subtractor_1 (.a(in_2), .b(5'b01111), .out(subtractor_1_out), .bout(_2));  // open: bin
  Multiplexer #(.width(5)) multiplexer_1 (
    .in0(subtractor_1_out), .in1({5{1'b0}}), .out({e4, e3, e2, e1, e0}), .sel(_2));  // open: en
  Multiplexer #(.width(32)) multiplexer_2 (
    .in0({32{1'b0}}), .in1(shifter_1_out), .out(_2_frac__1), .sel(in_3[9]));  // open: en
  Shifter #(.width(32), .shift("ar")) shifter_1 (.in(_2_frac), .\dist (5'b00001), .out(shifter_1_out));
  Multiplexer #(.width(32)) multiplexer_3 (
    .in0({32{1'b0}}), .in1(shifter_2_out), .out(_2_frac__2), .sel(in_3[8]));  // open: en
  Shifter #(.width(32), .shift("ar")) shifter_2 (.in(_2_frac), .\dist (5'b00010), .out(shifter_2_out));
  Multiplexer #(.width(32)) multiplexer_4 (
    .in0({32{1'b0}}), .in1(shifter_3_out), .out(_2_frac__3), .sel(in_3[7]));  // open: en
  Shifter #(.width(32), .shift("ar")) shifter_3 (.in(_2_frac), .\dist (5'b00011), .out(shifter_3_out));
  Multiplexer #(.width(32)) multiplexer_5 (
    .in0({32{1'b0}}), .in1(shifter_4_out), .out(_2_frac__4), .sel(in_3[6]));  // open: en
  Shifter #(.width(32), .shift("ar")) shifter_4 (.in(_2_frac), .\dist (5'b00100), .out(shifter_4_out));
  Multiplexer #(.width(32)) multiplexer_6 (
    .in0({32{1'b0}}), .in1(shifter_5_out), .out(_2_frac__5), .sel(in_3[5]));  // open: en
  Shifter #(.width(32), .shift("ar")) shifter_5 (.in(_2_frac), .\dist (5'b00101), .out(shifter_5_out));
  Multiplexer #(.width(32)) multiplexer_7 (
    .in0({32{1'b0}}), .in1(shifter_6_out), .out(_2_frac__6), .sel(in_3[4]));  // open: en
  Shifter #(.width(32), .shift("ar")) shifter_6 (.in(_2_frac), .\dist (5'b00110), .out(shifter_6_out));
  Multiplexer #(.width(32)) multiplexer_8 (
    .in0({32{1'b0}}), .in1(shifter_7_out), .out(_2_frac__7), .sel(in_3[3]));  // open: en
  Shifter #(.width(32), .shift("ar")) shifter_7 (.in(_2_frac), .\dist (5'b00111), .out(shifter_7_out));
  Multiplexer #(.width(32)) multiplexer_9 (
    .in0({32{1'b0}}), .in1(shifter_8_out), .out(_2_frac__8), .sel(in_3[2]));  // open: en
  Shifter #(.width(32), .shift("ar")) shifter_8 (.in(_2_frac), .\dist (5'b01000), .out(shifter_8_out));
  Multiplexer #(.width(32)) multiplexer_10 (
    .in0({32{1'b0}}), .in1(shifter_9_out), .out(_2_frac__9), .sel(in_3[1]));  // open: en
  Shifter #(.width(32), .shift("ar")) shifter_9 (.in(_2_frac), .\dist (5'b01001), .out(shifter_9_out));
  Multiplexer #(.width(32)) multiplexer_11 (
    .in0({32{1'b0}}), .in1(shifter_10_out), .out(_2_frac__10), .sel(in_3[0]));  // open: en
  Shifter #(.width(32), .shift("ar")) shifter_10 (.in(_2_frac), .\dist (5'b01010), .out(shifter_10_out));
  Multiplexer #(.width(32)) multiplexer_12 (.in0(32'h1), .in1(32'h2), .out(multiplexer_12_out), .sel(e0));  // open: en
  Multiplexer #(.width(32)) multiplexer_13 (.in0(32'h1), .in1(32'h4), .out(multiplexer_13_out), .sel(e1));  // open: en
  Multiplexer #(.width(32)) multiplexer_14 (.in0(32'h1), .in1(32'h10), .out(multiplexer_14_out), .sel(e2));  // open: en
  Multiplexer #(.width(32)) multiplexer_15 (
    .in0(32'h1), .in1(32'h100), .out(multiplexer_15_out), .sel(e3));  // open: en
  Multiplexer #(.width(32)) multiplexer_16 (
    .in0(32'h1), .in1(32'h10000), .out(multiplexer_16_out), .sel(e4));  // open: en
  Multiplier #(.width(32)) multiplier_1 (
    .a(multiplexer_12_out), .b(multiplexer_13_out), .out(multiplier_1_out));  // open: cin, cout
  Multiplier #(.width(32)) multiplier_2 (
    .a(multiplier_1_out), .b(multiplexer_14_out), .out(multiplier_2_out));  // open: cin, cout
  Multiplier #(.width(32)) multiplier_3 (
    .a(multiplier_2_out), .b(multiplexer_15_out), .out(multiplier_3_out));  // open: cin, cout
  Adder #(.width(32)) adder_1 (.a(_2_frac__1), .b(_2_frac__2), .out(adder_1_out));  // open: cin, cout
  Multiplier #(.width(32)) multiplier_4 (
    .a(multiplier_3_out), .b(multiplexer_16_out), .out(_2_frac));  // open: cin, cout
  Adder #(.width(32)) adder_2 (.a(adder_1_out), .b(_2_frac__3), .out(adder_2_out));  // open: cin, cout
  Adder #(.width(32)) adder_3 (.a(adder_2_out), .b(_2_frac__4), .out(adder_3_out));  // open: cin, cout
  Adder #(.width(32)) adder_4 (.a(adder_3_out), .b(_2_frac__5), .out(adder_4_out));  // open: cin, cout
  Adder #(.width(32)) adder_5 (.a(adder_4_out), .b(_2_frac__6), .out(adder_5_out));  // open: cin, cout
  Adder #(.width(32)) adder_6 (.a(adder_5_out), .b(_2_frac__7), .out(adder_6_out));  // open: cin, cout
  Adder #(.width(32)) adder_7 (.a(adder_6_out), .b(_2_frac__8), .out(adder_7_out));  // open: cin, cout
  Adder #(.width(32)) adder_8 (.a(adder_7_out), .b(_2_frac__9), .out(adder_8_out));  // open: cin, cout
  Adder #(.width(32)) adder_9 (.a(adder_8_out), .b(_2_frac__10), .out(adder_9_out));  // open: cin, cout
  Adder #(.width(32)) adder_10 (.a(_2_frac), .b(adder_9_out), .out(adder_10_out));  // open: cin, cout
  Negator #(.width(32)) negator_1 (.in(adder_10_out), .out(negator_1_out));
  Multiplexer #(.width(32)) multiplexer_17 (
    .in0(adder_10_out), .in1(negator_1_out), .out(multiplexer_17_out), .sel(in_1));  // open: en
  Multiplexer #(.width(32)) multiplexer_18 (
    .in0(multiplexer_17_out), .in1({32{1'b0}}), .out(out_4), .sel(_2));  // open: en

  // Other names for the same wires on the sheet: _10 = in_3[0]; _9 = in_3[1]; _8 = in_3[2]; _7 = in_3[3];
  //   _6 = in_3[4]; _5 = in_3[5]; _4 = in_3[6]; _3 = in_3[7]; _2_t = in_3[8]; _1 = in_3[9]; sign = in_1
endmodule
