// Logisim project gaizao.circ as structural Verilog: 3 circuits, main circuit fsm
module fsm (
  input  [1:0] in_1,
  input  in_2,
  output out_3
);

  wire clock_1_out, comparator_1_eq, comparator_2_gt, comparator_3_eq;
  wire [2:0] multiplexer_1_out, register_1_q, \状态转移_1_n0 ;
  wire [7:0] counter_1_q, register_2_q;

  Multiplexer #(.width(3)) multiplexer_1 (
    .in0(\状态转移_1_n0 ), .in1(3'b000), .out(multiplexer_1_out), .sel(in_2));  // open: en
  Register #(.width(3)) register_1 (.D(multiplexer_1_out), .Q(register_1_q), .clk(clock_1_out));  // open: en, clr
  Clock clock_1 (.out(clock_1_out));
  Counter counter_1 (.Q(counter_1_q), .clk(comparator_3_eq), .clr(comparator_1_eq));  // open: load, D, count, carry
  Comparator #(.width(3)) comparator_1 (.a(register_1_q), .b(3'b000), .eq(comparator_1_eq));  // open: gt, lt
  \状态转移  \u_状态转移_1  (
    .s2(register_1_q[2]), .s1(register_1_q[1]), .s0(register_1_q[0]), .in1(in_1[1]), .in0(in_1[0]),
    .n2(\状态转移_1_n0 [2]), .n1(\状态转移_1_n0 [1]), .n0(\状态转移_1_n0 [0]));
  m m_1 (.s2(register_1_q[2]), .s1(register_1_q[1]), .s0(register_1_q[0]), .in1(in_1[1]), .in0(in_1[0]), .o(out_3));
  Register register_2 (.D(counter_1_q), .en(comparator_2_gt), .Q(register_2_q), .clk(clock_1_out));  // open: clr
  Comparator comparator_2 (.a(counter_1_q), .b(register_2_q), .gt(comparator_2_gt));  // open: eq, lt
  Comparator #(.width(3)) comparator_3 (.a(register_1_q), .b(3'b100), .eq(comparator_3_eq));  // open: gt, lt
endmodule

module \状态转移  (
  input  s2,
  input  s1,
  input  s0,
  input  in1,
  input  in0,
  output n2,
  output n1,
  output n0
);

  wire and_2_out, and_3_out, and_4_out, and_5_out, and_6_out, and_7_out, and_8_out, and_9_out, not_1_out,
       not_2_out, not_3_out, not_4_out, not_5_out, not_6_out, not_7_out, not_8_out, not_9_out, not_10_out,
       not_11_out, not_12_out, not_13_out, not_14_out, not_15_out, not_16_out, not_17_out, not_18_out,
       not_19_out, not_20_out, not_21_out, not_22_out, not_23_out, not_24_out, not_25_out;

  not not_1 (not_1_out, s2);
  not not_2 (not_2_out, in0);
  not not_3 (not_3_out, s2);
  not not_4 (not_4_out, s1);
  not not_5 (not_5_out, in1);
  not not_6 (not_6_out, s2);
  not not_7 (not_7_out, s1);
  not not_8 (not_8_out, in0);
  not not_9 (not_9_out, s2);
  not not_10 (not_10_out, s0);
  not not_11 (not_11_out, in1);
  not not_12 (not_12_out, s2);
  not not_13 (not_13_out, s0);
  not not_14 (not_14_out, in0);
  not not_15 (not_15_out, s1);
  not not_16 (not_16_out, s0);
  not not_17 (not_17_out, in1);
  not not_18 (not_18_out, s2);
  not not_19 (not_19_out, s1);
  not not_20 (not_20_out, in0);
  not not_21 (not_21_out, s2);
  not not_22 (not_22_out, s0);
  not not_23 (not_23_out, in0);
  not not_24 (not_24_out, s2);
  not not_25 (not_25_out, in1);
  and and_1 (n2, not_1_out, s1, s0, not_2_out);
  and and_2 (and_2_out, not_3_out, not_4_out, s0, not_5_out);
  and and_3 (and_3_out, not_6_out, not_7_out, s0, not_8_out);
  and and_4 (and_4_out, not_9_out, s1, not_10_out, not_11_out);
  and and_5 (and_5_out, not_12_out, s1, not_13_out, not_14_out);
  and and_6 (and_6_out, not_15_out, not_16_out, not_17_out, in0);
  and and_7 (and_7_out, not_18_out, not_19_out, s0, not_20_out);
  and and_8 (and_8_out, not_21_out, s1, not_22_out, not_23_out);
  and and_9 (and_9_out, not_24_out, s1, s0, not_25_out, in0);
  or or_1 (n1, and_2_out, and_3_out, and_4_out, and_5_out);
  or or_2 (n0, and_6_out, and_7_out, and_8_out, and_9_out);
endmodule

module m (
  input  s2,
  input  s1,
  input  s0,
  input  in1,
  input  in0,
  output o
);

  wire not_1_out, not_2_out;

  not not_1 (not_1_out, s2);
  not not_2 (not_2_out, in0);
  and and_1 (o, not_1_out, s1, s0, not_2_out);
endmodule
