// Logisim project hhh.circ as structural Verilog: 3 circuits, main circuit main
module main (
  input  A,
  input  B,
  input  C,
  input  D,
  input  E,
  output q
);

  wire and_1_out, and_2_out, and_3_out, and_4_out, ct74151_1_out_12, ct74151_2_out_12, ct74151_3_out_12,
       ct74151_4_out_12, not_1_out, not_2_out, not_3_out, not_4_out;

  CT74151 ct74151_1 (
    ._8(1'b0), .in_2(1'b1), .in_3(1'b0), .in_4(1'b1), .in_5(1'b0), .in_6(1'b1), .in_7(1'b0), .in_8(1'b1),
    .out_12(ct74151_1_out_12), .in_9(C), .in_10(D), .in_11(E));
  CT74151 ct74151_2 (
    ._8(1'b1), .in_2(1'b0), .in_3(1'b1), .in_4(1'b0), .in_5(1'b1), .in_6(1'b0), .in_7(1'b1), .in_8(1'b0),
    .out_12(ct74151_2_out_12), .in_9(C), .in_10(D), .in_11(E));
  CT74151 ct74151_3 (
    ._8(1'b1), .in_2(1'b1), .in_3(1'b1), .in_4(1'b1), .in_5(1'b1), .in_6(1'b1), .in_7(1'b1), .in_8(1'b1),
    .out_12(ct74151_3_out_12), .in_9(C), .in_10(D), .in_11(E));
  CT74151 ct74151_4 (
    ._8(1'b0), .in_2(1'b0), .in_3(1'b0), .in_4(1'b0), .in_5(1'b0), .in_6(1'b0), .in_7(1'b0), .in_8(1'b0),
    .out_12(ct74151_4_out_12), .in_9(C), .in_10(D), .in_11(E));
  not not_1 (not_1_out, A);
  not not_2 (not_2_out, B);
  not not_3 (not_3_out, B);
  not not_4 (not_4_out, A);
  and and_1 (and_1_out, ct74151_4_out_12, B, A);
  and and_2 (and_2_out, ct74151_3_out_12, B, not_1_out);
  and and_3 (and_3_out, ct74151_2_out_12, not_2_out, A);
  and and_4 (and_4_out, ct74151_1_out_12, not_3_out, not_4_out);
  or or_1 (q, and_1_out, and_2_out, and_3_out, and_4_out);

  // Notes on the sheet:
  //   8
  //   15:8
  //   23:16
  //   31:24
endmodule

module CT74151 (
  input  _8,
  input  in_2,
  input  in_3,
  input  in_4,
  input  in_5,
  input  in_6,
  input  in_7,
  input  in_8,
  input  in_9,
  input  in_10,
  input  in_11,
  output out_12
);

  Multiplexer #(.select(3)) multiplexer_1 (
    .in0(_8), .in1(in_2), .in2(in_3), .in3(in_4), .in4(in_5), .in5(in_6), .in6(in_7), .in7(in_8),
    .out(out_12), .sel({in_9, in_10, in_11}));  // open: en
endmodule

module mux (
  input  d0,
  input  d1,
  input  d2,
  input  d3,
  input  c0,
  input  c1,
  output q
);

  wire and_1_out, and_2_out, and_3_out, and_4_out, not_1_out, not_2_out, not_3_out, not_4_out;

  not not_1 (not_1_out, c1);
  not not_2 (not_2_out, c0);
  not not_3 (not_3_out, c0);
  not not_4 (not_4_out, c1);
  and and_1 (and_1_out, d3, c0, c1);
  and and_2 (and_2_out, d2, c0, not_1_out);
  and and_3 (and_3_out, d1, not_2_out, c1);
  and and_4 (and_4_out, d0, not_3_out, not_4_out);
  or or_1 (q, and_1_out, and_2_out, and_3_out, and_4_out);
endmodule
