// Logisim project md5加密.circ as structural Verilog: 1 circuit, main circuit main
module main (
  input  [31:0] in_1,
  output [31:0] out_2
);

  wire [4:0] bitfinder_1_index, bitfinder_2_index, negator_1_out, subtractor_1_out, subtractor_2_out,
       subtractor_3_out;
  wire [31:0] bit_extender_1_out, or_1_out, shifter_1_out, shifter_2_out, shifter_3_out, shifter_4_out,
       shifter_5_out, xor_1_out;

  BitFinder #(.width(32), .\type ("high1")) bitfinder_1 (.in(in_1), .index(bitfinder_1_index));  // open: found
  Subtractor #(.width(5)) subtractor_1 (
    .a(bitfinder_1_index), .b(5'b00100), .out(subtractor_1_out));  // open: bin, bout
  Shifter #(.width(32)) shifter_1 (.in(32'h15), .\dist (subtractor_1_out), .out(shifter_1_out));
  assign xor_1_out = in_1 ^ shifter_1_out;  // XOR_Gate xor_1, 32 bits wide
  BitFinder #(.width(32), .\type ("high1")) bitfinder_2 (.in(xor_1_out), .index(bitfinder_2_index));  // open: found
  Negator #(.width(5)) negator_1 (.in(bitfinder_2_index), .out(negator_1_out));
  Comparator #(.width(5), .mode("unsigned")) comparator_1 (.a(bitfinder_2_index), .b(5'b11011));  // open: gt, eq, lt
  Subtractor #(.width(5)) subtractor_2 (.a(negator_1_out), .b(5'b00001), .out(subtractor_2_out));  // open: bin, bout
  Shifter #(.width(32)) shifter_2 (.in(xor_1_out), .\dist (subtractor_2_out), .out(shifter_2_out));
  Subtractor #(.width(5)) subtractor_3 (.a(subtractor_2_out), .b(5'b00001), .out(subtractor_3_out));  // open: bin, bout
  Shifter #(.width(32)) shifter_3 (.in(32'h1), .\dist (subtractor_3_out), .out(shifter_3_out));
  assign or_1_out = shifter_2_out | shifter_3_out;  // OR_Gate or_1, 32 bits wide
  Shifter #(.width(32), .shift("lr")) shifter_4 (.in(or_1_out), .\dist (5'b00101), .out(shifter_4_out));
  assign bit_extender_1_out = {{27{1'b0}}, bitfinder_2_index};  // Bit_Extender bit_extender_1
  assign out_2 = shifter_4_out | shifter_5_out;  // OR_Gate or_2, 32 bits wide
  Shifter #(.width(32)) shifter_5 (.in(bit_extender_1_out), .\dist (5'b11011), .out(shifter_5_out));
  Divider divider_1 ();  // open: a, b, out, upper, rem
endmodule
