// Logisim project mod5.circ as structural Verilog: 4 circuits, main circuit state_trans
module state_trans (
  input  new_bit,
  input  s1,
  input  s0,
  output ss1,
  output ss0
);

  wire and_1_out, and_2_out, and_3_out, and_4_out, and_5_out, and_6_out, not_1_out, not_2_out, not_3_out,
       not_4_out, not_5_out, not_6_out, not_7_out, not_8_out;

  not not_1 (not_1_out, s1);
  not not_2 (not_2_out, s0);
  not not_3 (not_3_out, new_bit);
  not not_4 (not_4_out, s1);
  not not_5 (not_5_out, new_bit);
  not not_6 (not_6_out, s0);
  not not_7 (not_7_out, s1);
  not not_8 (not_8_out, s0);
  and and_1 (and_1_out, not_1_out, s0);
  and and_2 (and_2_out, s1, not_2_out);
  and and_3 (and_3_out, not_3_out, not_4_out, s0);
  and and_4 (and_4_out, not_5_out, s1, not_6_out);
  and and_5 (and_5_out, new_bit, not_7_out, not_8_out);
  and and_6 (and_6_out, new_bit, s1, s0);
  or or_1 (ss1, and_1_out, and_2_out);
  or or_2 (ss0, and_3_out, and_4_out, and_5_out, and_6_out);
endmodule

module mod5 (
  input  in_1,
  output _0,
  output _1,
  output _2,
  output _3,
  output _4
);

  wire clock_1_out;
  wire [1:0] register_1_q, state_trans_1_ss0;

  // Probe on register_1_q
  state_trans state_trans_1 (
    .new_bit(in_1), .s1(register_1_q[1]), .s0(register_1_q[0]), .ss1(state_trans_1_ss0[1]),
    .ss0(state_trans_1_ss0[0]));
  // Probe on state_trans_1_ss0
  Register #(.width(2)) register_1 (.D(state_trans_1_ss0), .Q(register_1_q), .clk(clock_1_out));  // open: en, clr
  Clock clock_1 (.out(clock_1_out));
  deco deco_1 (.in1(register_1_q[1]), .in0(register_1_q[0]), .b(in_1), .s0(_0), .s1(_1), .s2(_2), .s3(_3), .s4(_4));
endmodule

module init (
  input  In,
  output s1,
  output s2,
  output s3
);

  not not_1 (s3, In);

  assign s1 = 1'b0;
  assign s2 = In;
endmodule

module deco (
  input  in1,
  input  in0,
  input  b,
  output s0,
  output s1,
  output s2,
  output s3,
  output s4
);

  wire and_1_out, and_2_out, and_3_out, and_4_out, and_5_out, and_6_out, and_7_out, and_8_out, not_1_out,
       not_2_out, not_3_out, not_4_out, not_5_out, not_6_out, not_7_out, not_8_out, not_9_out, not_10_out,
       not_11_out, not_12_out;

  not not_1 (not_1_out, in1);
  not not_2 (not_2_out, in0);
  not not_3 (not_3_out, b);
  not not_4 (not_4_out, b);
  not not_5 (not_5_out, in1);
  not not_6 (not_6_out, in0);
  not not_7 (not_7_out, in1);
  not not_8 (not_8_out, in0);
  not not_9 (not_9_out, in1);
  not not_10 (not_10_out, b);
  not not_11 (not_11_out, in0);
  not not_12 (not_12_out, b);
  and and_1 (and_1_out, not_1_out, not_2_out, not_3_out);
  and and_2 (and_2_out, in1, in0, not_4_out);
  and and_3 (and_3_out, not_5_out, not_6_out, b);
  and and_4 (and_4_out, in1, in0, b);
  and and_5 (and_5_out, not_7_out, in0, b);
  and and_6 (and_6_out, in1, not_8_out, b);
  and and_7 (and_7_out, not_9_out, in0, not_10_out);
  and and_8 (and_8_out, in1, not_11_out, not_12_out);
  or or_1 (s1, and_1_out, and_2_out);
  or or_2 (s2, and_3_out, and_4_out);
  or or_3 (s3, and_5_out, and_6_out);
  or or_4 (s4, and_7_out, and_8_out);

  assign s0 = 1'b0;
endmodule
