// Logisim project navigation.circ as structural Verilog: 3 circuits, main circuit navigation
module navigation (
  input  in_1,
  input  in_2,
  input  [1:0] in_3,
  output out_4,
  output out_5
);

  wire state_trans_1_hit;
  wire [2:0] register_1_q, state_trans_1_ns2;

  Register #(.width(3)) register_1 (.D(state_trans_1_ns2), .Q(register_1_q), .clk(in_1), .clr(in_2));  // open: en
  state_trans state_trans_1 (
    .cs0(register_1_q[2]), .cs1(register_1_q[1]), .cs2(register_1_q[0]), .dir0(in_3[1]), .dir1(in_3[0]),
    .ns0(state_trans_1_ns2[2]), .ns1(state_trans_1_ns2[1]), .ns2(state_trans_1_ns2[0]),
    .hit(state_trans_1_hit));
  Comparator #(.width(3)) comparator_1 (.a(register_1_q), .b(3'b001), .eq(out_4));  // open: gt, lt
  Register #(.width(1)) register_2 (.D(state_trans_1_hit), .Q(out_5), .clk(in_1), .clr(in_2));  // open: en
endmodule

module state_trans (
  input  cs0,
  input  cs1,
  input  cs2,
  input  dir0,
  input  dir1,
  output ns0,
  output ns1,
  output ns2,
  output hit
);

  wire and_1_out, and_2_out, and_3_out, and_4_out, and_5_out, and_6_out, and_7_out, and_8_out, and_9_out,
       and_10_out, and_11_out, and_12_out, and_13_out, and_14_out, and_15_out, and_16_out, not_1_out,
       not_2_out, not_3_out, not_4_out, not_5_out, not_6_out, not_7_out, not_8_out, not_9_out, not_10_out,
       not_11_out, not_12_out, not_13_out, not_14_out, not_15_out, not_16_out, not_17_out, not_18_out,
       not_19_out, not_20_out, not_21_out, not_22_out, not_23_out, not_24_out, not_25_out, not_26_out,
       not_27_out, not_28_out, not_29_out, not_30_out, not_31_out, not_32_out, not_33_out, not_34_out,
       not_35_out, not_36_out, not_37_out, not_38_out, not_39_out, not_40_out, not_41_out, not_42_out,
       not_43_out, not_44_out;

  not not_1 (not_1_out, cs0);
  not not_2 (not_2_out, dir0);
  not not_3 (not_3_out, dir1);
  not not_4 (not_4_out, cs1);
  not not_5 (not_5_out, cs2);
  not not_6 (not_6_out, dir0);
  not not_7 (not_7_out, dir1);
  not not_8 (not_8_out, cs1);
  not not_9 (not_9_out, cs2);
  not not_10 (not_10_out, cs0);
  not not_11 (not_11_out, cs1);
  not not_12 (not_12_out, cs2);
  not not_13 (not_13_out, dir0);
  not not_14 (not_14_out, dir1);
  not not_15 (not_15_out, cs0);
  not not_16 (not_16_out, cs0);
  not not_17 (not_17_out, cs2);
  not not_18 (not_18_out, cs1);
  not not_19 (not_19_out, cs2);
  not not_20 (not_20_out, dir1);
  not not_21 (not_21_out, cs0);
  not not_22 (not_22_out, cs2);
  not not_23 (not_23_out, dir0);
  not not_24 (not_24_out, dir1);
  not not_25 (not_25_out, cs0);
  not not_26 (not_26_out, cs1);
  not not_27 (not_27_out, cs2);
  not not_28 (not_28_out, dir0);
  not not_29 (not_29_out, cs1);
  not not_30 (not_30_out, cs2);
  not not_31 (not_31_out, dir1);
  not not_32 (not_32_out, cs0);
  not not_33 (not_33_out, cs2);
  not not_34 (not_34_out, dir0);
  not not_35 (not_35_out, cs0);
  not not_36 (not_36_out, cs2);
  not not_37 (not_37_out, dir1);
  not not_38 (not_38_out, cs1);
  not not_39 (not_39_out, cs2);
  not not_40 (not_40_out, cs0);
  not not_41 (not_41_out, cs1);
  not not_42 (not_42_out, cs2);
  not not_43 (not_43_out, dir0);
  not not_44 (not_44_out, dir1);
  and and_1 (and_1_out, not_1_out, cs1, cs2, not_2_out, not_3_out);
  and and_2 (and_2_out, cs0, not_4_out, not_5_out, not_6_out, not_7_out);
  and and_3 (and_3_out, cs0, not_8_out, not_9_out, dir0, dir1);
  and and_4 (and_4_out, not_10_out, not_11_out, not_12_out, not_13_out, not_14_out);
  and and_5 (and_5_out, not_15_out, cs1, dir1);
  and and_6 (and_6_out, not_16_out, cs1, not_17_out, dir0);
  and and_7 (and_7_out, cs0, not_18_out, not_19_out, dir0, not_20_out);
  and and_8 (and_8_out, not_21_out, not_22_out, not_23_out, not_24_out);
  and and_9 (and_9_out, not_25_out, cs1, dir0, dir1);
  and and_10 (and_10_out, cs0, not_26_out, not_27_out, not_28_out, dir1);
  and and_11 (and_11_out, cs0, not_29_out, not_30_out, dir0, not_31_out);
  and and_12 (and_12_out, not_32_out, not_33_out, not_34_out, dir1);
  and and_13 (and_13_out, not_35_out, not_36_out, dir0, not_37_out);
  and and_14 (and_14_out, not_38_out, not_39_out, dir0, dir1);
  and and_15 (and_15_out, not_40_out, cs1, cs2, dir0, dir1);
  and and_16 (and_16_out, cs0, not_41_out, not_42_out, not_43_out, not_44_out);
  or or_1 (ns0, and_1_out, and_2_out, and_3_out);
  or or_2 (ns1, and_4_out, and_5_out, and_6_out, and_7_out);
  or or_3 (ns2, and_8_out, and_9_out, and_10_out, and_11_out);
  or or_4 (hit, and_12_out, and_13_out, and_14_out, and_15_out, and_16_out);
endmodule

module test (
  input  [1:0] s,
  input  s_2,
  output ns0,
  output ns0_2
);

  wire clock_1_out;

  Clock clock_1 (.out(clock_1_out));
  navigation navigation_1 (.out_4(ns0), .out_5(ns0_2), .in_2(s_2), .in_3(s), .in_1(clock_1_out));
endmodule
