// Logisim project shishi.circ as structural Verilog: 1 circuit, main circuit main
module main (
  input  [31:0] in_1,
  input  [31:0] in_2,
  output [31:0] out_3
);

  wire [31:0] and_1_out, or_1_out;

  // Probe on in_1
  assign or_1_out = in_1 | in_2;  // OR_Gate or_1, 32 bits wide
  assign and_1_out = in_1 & in_2;  // AND_Gate and_1, 32 bits wide
  assign out_3 = and_1_out | or_1_out;  // OR_Gate or_2, 32 bits wide
endmodule
