// Logisim project shishikan.circ as structural Verilog: 2 circuits, main circuit main
module main (
  input  [2:0] in_1,
  output [3:0] out_2
);

  wire clock_1_out, comparator_1_eq;
  wire [3:0] bit_extender_1_out, counter_1_q;

  Counter #(.width(4), .max('hf)) counter_1 (
    .count(1'b1), .Q(counter_1_q), .clk(clock_1_out));  // open: load, D, carry, clr
  Clock clock_1 (.out(clock_1_out));
  cal cal_1 (.in_2(comparator_1_eq), .out_3(out_2));  // open: in_1
  assign bit_extender_1_out = {{1{1'b0}}, in_1};  // Bit_Extender bit_extender_1
  Comparator #(.width(4)) comparator_1 (.a(bit_extender_1_out), .b(counter_1_q), .eq(comparator_1_eq));  // open: gt, lt
endmodule

module cal (
  input  in_1,
  input  in_2,
  output [3:0] out_3
);

  wire clock_1_out, counter_1_q, not_1_out;
  wire [3:0] adder_1_out, multiplexer_1_out, prev_q;

  Counter #(.width(1), .max('h1), .ongoal("stay")) counter_1 (
    .count(clock_1_out), .Q(counter_1_q), .clr(in_1));  // open: load, D, carry, clk
  Clock clock_1 (.out(clock_1_out));
  Multiplexer #(.width(4)) multiplexer_1 (
    .in0(4'b0001), .in1(out_3), .out(multiplexer_1_out), .sel(counter_1_q));  // open: en
  Register #(.width(4)) prev (.D(multiplexer_1_out), .en(clock_1_out), .Q(prev_q), .clk(not_1_out));  // open: clr
  Register #(.width(4)) \new  (.D(adder_1_out), .en(clock_1_out), .Q(out_3), .clk(not_1_out), .clr(in_1));
  not not_1 (not_1_out, in_2);
  Adder #(.width(4)) adder_1 (.a(prev_q), .b(out_3), .out(adder_1_out));  // open: cin, cout
endmodule
