// Logisim project state_tran.circ as structural Verilog: 2 circuits, main circuit main
module main (
  input  in_1,
  output s0,
  output s1,
  output s2,
  output s3,
  output s4
);

  mod5 mod5_1 (.in_1(in_1), ._0(s0), ._1(s1), ._2(s2), ._3(s3), ._4(s4));
endmodule

module state_trans (
  input  new_bit,
  input  s1,
  input  s0,
  output ss1,
  output ss0
);

  wire and_1_out, and_2_out, and_3_out, and_4_out, and_5_out, and_6_out, not_1_out, not_2_out, not_3_out,
       not_4_out, not_5_out, not_6_out, not_7_out, not_8_out;

  not not_1 (not_1_out, s1);
  not not_2 (not_2_out, s0);
  not not_3 (not_3_out, new_bit);
  not not_4 (not_4_out, s1);
  not not_5 (not_5_out, new_bit);
  not not_6 (not_6_out, s0);
  not not_7 (not_7_out, s1);
  not not_8 (not_8_out, s0);
  and and_1 (and_1_out, not_1_out, s0);
  and and_2 (and_2_out, s1, not_2_out);
  and and_3 (and_3_out, not_3_out, not_4_out, s0);
  and and_4 (and_4_out, not_5_out, s1, not_6_out);
  and and_5 (and_5_out, new_bit, not_7_out, not_8_out);
  and and_6 (and_6_out, new_bit, s1, s0);
  or or_1 (ss1, and_1_out, and_2_out);
  or or_2 (ss0, and_3_out, and_4_out, and_5_out, and_6_out);
endmodule
