// Logisim project state_trans.circ as structural Verilog: 2 circuits, main circuit state_trans
module state_trans (
  input  new_bit,
  input  s1,
  input  s2,
  input  s3,
  output s1_2,
  output s2_2,
  output s3_2
);

  wire and_2_out, and_3_out, and_4_out, and_5_out, and_6_out, and_7_out, not_1_out, not_2_out, not_3_out,
       not_4_out;

  not not_1 (not_1_out, new_bit);
  and and_1 (s1_2, not_1_out, s2);
  and and_2 (and_2_out, new_bit, s3);
  and and_3 (and_3_out, new_bit, s2);
  and and_4 (and_4_out, new_bit, s1);
  not not_2 (not_2_out, new_bit);
  not not_3 (not_3_out, s2);
  and and_5 (and_5_out, not_2_out, not_3_out, s3);
  not not_4 (not_4_out, new_bit);
  and and_6 (and_6_out, not_4_out, s1);
  and and_7 (and_7_out, new_bit, s2);
  or or_1 (s2_2, and_2_out, and_3_out, and_4_out);
  or or_2 (s3_2, and_5_out, and_6_out, and_7_out);
endmodule

module whole (
  input  in_1
);

  wire clock_1_out;
  wire [2:0] register_1_q, state_trans_1_s1_2;

  state_trans state_trans_1 (
    .new_bit(in_1), .s1(register_1_q[0]), .s2(register_1_q[1]), .s3(register_1_q[2]),
    .s1_2(state_trans_1_s1_2[0]), .s2_2(state_trans_1_s1_2[1]), .s3_2(state_trans_1_s1_2[2]));
  // Probe on state_trans_1_s1_2
  Register #(.width(3)) register_1 (.D(state_trans_1_s1_2), .Q(register_1_q), .clk(clock_1_out));  // open: en, clr
  Clock clock_1 (.out(clock_1_out));
  Decoder #(.select(3)) decoder_1 ();  // open: out0, out1, out2, out3, out4, out5, out6, out7, sel, en
endmodule
