// Logisim project test.circ as structural Verilog: 1 circuit, main circuit main
module main (
);

  wire clock_1_out, fsm_1_out_3, fsm_2_p4;
  wire [2:0] rom_1_data;
  wire [7:0] counter_1_q;

  Counter counter_1 (.Q(counter_1_q), .clk(clock_1_out), .clr(clock_1_out));  // open: load, D, count, carry
  ROM #(.dataWidth(3)) rom_1 (.addr(counter_1_q), .data(rom_1_data));  // open: sel
  Clock clock_1 (.out(clock_1_out));
  fsm fsm_1 (.in_2(rom_1_data[1:0]), .in_1(rom_1_data[2]), .out_3(fsm_1_out_3));
  // fsm fsm_2: pin names not known; wires that end beside it: clock_1_out, rom_1_data[1:0], rom_1_data[2], fsm_2_p4, fsm_1_out_3, fsm_2_p4

  // Notes on the sheet:
  //   in
endmodule
