// Logisim project voter.circ as structural Verilog: 1 circuit, main circuit main
module main (
  input  a,
  input  b,
  input  c,
  output pass
);

  wire and_1_out, and_2_out, and_3_out;

  and and_1 (and_1_out, b, c);
  and and_2 (and_2_out, a, c);
  and and_3 (and_3_out, a, b);
  or or_1 (pass, and_1_out, and_2_out, and_3_out);
endmodule
