// Logisim project P0_L0_GRF.circ as structural Verilog: 2 circuits, main circuit grf
module grf (
  input  in_1,
  input  in_2,
  input  in_3,
  input  [4:0] A1,
  input  [4:0] A2,
  input  [4:0] A3,
  input  [31:0] WD,
  output [31:0] RD1,
  output [31:0] RD2
);

  wire [31:0] _0out, _1in, _1out, _2in, _2out, _3in, _3out, _4in, _4out, _5in, _5out, _6in, _6out, _7in,
       _7out, _8in, _8out, _9in, _9out, _10in, _10out, _11in, _11out, _12in, _12out, _13in, _13out, _14in,
       _14out, _15in, _15out, _16in, _16out, _17in, _17out, _18in, _18out, _19in, _19out, _20in, _20out,
       _21in, _21out, _22in, _22out, _23in, _23out, _24in, _24out, _25in, _25out, _26in, _26out, _27in,
       _27out, _28in, _28out, _29in, _29out, _30in, _30out, _31in, _31out;

  Register #(.width(32)) _0 (.D({32{1'b0}}), .Q(_0out), .clk(in_1), .clr(in_2));  // open: en
  Register #(.width(32)) _1 (.D(_1in), .Q(_1out), .clk(in_1), .clr(in_2));  // open: en
  Register #(.width(32)) _2 (.D(_2in), .Q(_2out), .clk(in_1), .clr(in_2));  // open: en
  Register #(.width(32)) _3 (.D(_3in), .Q(_3out), .clk(in_1), .clr(in_2));  // open: en
  Multiplexer #(.select(5), .width(32), .disabled(0)) multiplexer_1 (
    .in0(_0out), .in1(_1out), .in2(_2out), .in3(_3out), .in4(_4out), .in5(_5out), .in6(_6out), .in7(_7out),
    .in8(_8out), .in9(_9out), .in10(_10out), .in11(_11out), .in12(_12out), .in13(_13out), .in14(_14out),
    .in15(_15out), .in16(_16out), .in17(_17out), .in18(_18out), .in19(_19out), .in20(_20out), .in21(_21out),
    .in22(_22out), .in23(_23out), .in24(_24out), .in25(_25out), .in26(_26out), .in27(_27out), .in28(_28out),
    .in29(_29out), .in30(_30out), .in31(_31out), .out(RD1), .sel(A1));  // open: en
  Register #(.width(32)) _4 (.D(_4in), .Q(_4out), .clk(in_1), .clr(in_2));  // open: en
  Register #(.width(32)) _5 (.D(_5in), .Q(_5out), .clk(in_1), .clr(in_2));  // open: en
  Register #(.width(32)) _6 (.D(_6in), .Q(_6out), .clk(in_1), .clr(in_2));  // open: en
  Register #(.width(32)) _7 (.D(_7in), .Q(_7out), .clk(in_1), .clr(in_2));  // open: en
  Multiplexer #(.select(5), .width(32), .disabled(0)) multiplexer_2 (
    .in0(_0out), .in1(_1out), .in2(_2out), .in3(_3out), .in4(_4out), .in5(_5out), .in6(_6out), .in7(_7out),
    .in8(_8out), .in9(_9out), .in10(_10out), .in11(_11out), .in12(_12out), .in13(_13out), .in14(_14out),
    .in15(_15out), .in16(_16out), .in17(_17out), .in18(_18out), .in19(_19out), .in20(_20out), .in21(_21out),
    .in22(_22out), .in23(_23out), .in24(_24out), .in25(_25out), .in26(_26out), .in27(_27out), .in28(_28out),
    .in29(_29out), .in30(_30out), .in31(_31out), .out(RD2), .sel(A2));  // open: en
  Register #(.width(32)) _8 (.D(_8in), .Q(_8out), .clk(in_1), .clr(in_2));  // open: en
  Register #(.width(32)) _9 (.D(_9in), .Q(_9out), .clk(in_1), .clr(in_2));  // open: en
  Register #(.width(32)) _10 (.D(_10in), .Q(_10out), .clk(in_1), .clr(in_2));  // open: en
  Register #(.width(32)) _11 (.D(_11in), .Q(_11out), .clk(in_1), .clr(in_2));  // open: en
  Demultiplexer #(.select(5), .width(32), .tristate("true"), .disabled(0)) demultiplexer_1 (
    .out1(_1in), .out2(_2in), .out3(_3in), .out4(_4in), .out5(_5in), .out6(_6in), .out7(_7in), .out8(_8in),
    .out9(_9in), .out10(_10in), .out11(_11in), .out12(_12in), .out13(_13in), .out14(_14in), .out15(_15in),
    .out16(_16in), .out17(_17in), .out18(_18in), .out19(_19in), .out20(_20in), .out21(_21in), .out22(_22in),
    .out23(_23in), .out24(_24in), .out25(_25in), .out26(_26in), .out27(_27in), .out28(_28in), .out29(_29in),
    .out30(_30in), .out31(_31in), .in(WD), .sel(A3), .en(in_3));  // open: out0
  Register #(.width(32)) _12 (.D(_12in), .Q(_12out), .clk(in_1), .clr(in_2));  // open: en
  Register #(.width(32)) _13 (.D(_13in), .Q(_13out), .clk(in_1), .clr(in_2));  // open: en
  Register #(.width(32)) _14 (.D(_14in), .Q(_14out), .clk(in_1), .clr(in_2));  // open: en
  Register #(.width(32)) _15 (.D(_15in), .Q(_15out), .clk(in_1), .clr(in_2));  // open: en
  Register #(.width(32)) _16 (.D(_16in), .Q(_16out), .clk(in_1), .clr(in_2));  // open: en
  Register #(.width(32)) _17 (.D(_17in), .Q(_17out), .clk(in_1), .clr(in_2));  // open: en
  Register #(.width(32)) _18 (.D(_18in), .Q(_18out), .clk(in_1), .clr(in_2));  // open: en
  Register #(.width(32)) _19 (.D(_19in), .Q(_19out), .clk(in_1), .clr(in_2));  // open: en
  Register #(.width(32)) _20 (.D(_20in), .Q(_20out), .clk(in_1), .clr(in_2));  // open: en
  Register #(.width(32)) _21 (.D(_21in), .Q(_21out), .clk(in_1), .clr(in_2));  // open: en
  Register #(.width(32)) _22 (.D(_22in), .Q(_22out), .clk(in_1), .clr(in_2));  // open: en
  Register #(.width(32)) _23 (.D(_23in), .Q(_23out), .clk(in_1), .clr(in_2));  // open: en
  Register #(.width(32)) _24 (.D(_24in), .Q(_24out), .clk(in_1), .clr(in_2));  // open: en
  Register #(.width(32)) _25 (.D(_25in), .Q(_25out), .clk(in_1), .clr(in_2));  // open: en
  Register #(.width(32)) _26 (.D(_26in), .Q(_26out), .clk(in_1), .clr(in_2));  // open: en
  Register #(.width(32)) _27 (.D(_27in), .Q(_27out), .clk(in_1), .clr(in_2));  // open: en
  Register #(.width(32)) _28 (.D(_28in), .Q(_28out), .clk(in_1), .clr(in_2));  // open: en
  Register #(.width(32)) _29 (.D(_29in), .Q(_29out), .clk(in_1), .clr(in_2));  // open: en
  Register #(.width(32)) _30 (.D(_30in), .Q(_30out), .clk(in_1), .clr(in_2));  // open: en
  Register #(.width(32)) _31 (.D(_31in), .Q(_31out), .clk(in_1), .clr(in_2));  // open: en

  // Other names for the same wires on the sheet: clk = in_1; reset = in_2; WE = in_3
endmodule

module test (
  output [31:0] RD1,
  output [31:0] RD2,
  output out_3
);

  wire clock_1_out;
  wire [7:0] counter_1_q;
  wire [16:0] rom_1_data;
  wire [31:0] rom_2_data;

  Clock clock_1 (.out(clock_1_out));
  Counter #(.max('h3)) counter_1 (.Q(counter_1_q), .carry(out_3), .clk(clock_1_out));  // open: load, D, count, clr
  ROM #(.dataWidth(17)) rom_1 (.addr(counter_1_q), .data(rom_1_data));  // open: sel
  ROM #(.dataWidth(32)) rom_2 (.addr(counter_1_q), .data(rom_2_data));  // open: sel
  grf grf_1 (
    .A1(rom_1_data[14:10]), .A2(rom_1_data[9:5]), .A3(rom_1_data[4:0]), .WD(rom_2_data), .in_1(clock_1_out),
    .in_2(rom_1_data[16]), .in_3(rom_1_data[15]), .RD1(RD1), .RD2(RD2));

  // Notes on the sheet:
  //   contents of rom_1 (hex, n*v repeats v):
  //   8021 8822 822
  //   contents of rom_2 (hex, n*v repeats v):
  //   10203430 ffffff 112233 44556677 8899aabb 3333 4444 1
endmodule
