// Logisim project fsm.circ as structural Verilog: 5 circuits, main circuit fsm
module fsm (
  input  in_1,
  input  [1:0] in_2,
  output out_3
);

  wire clock_1_out, meely1_1_o, meely2_1_o;
  wire [2:0] register_1_q, register_2_q, state_trans1_1_n0, state_trans2_1_n0;

  Register #(.width(3)) register_1 (
    .D(state_trans1_1_n0), .Q(register_1_q), .clk(clock_1_out), .clr(in_1));  // open: en
  Register #(.width(3)) register_2 (
    .D(state_trans2_1_n0), .Q(register_2_q), .clk(clock_1_out), .clr(in_1));  // open: en
  Clock clock_1 (.out(clock_1_out));
  meely1 meely1_1 (
    .s2(register_1_q[2]), .s1(register_1_q[1]), .s0(register_1_q[0]), .in1(in_2[1]), .in0(in_2[0]),
    .o(meely1_1_o));
  state_trans1 state_trans1_1 (
    .s2(register_1_q[2]), .s1(register_1_q[1]), .s0(register_1_q[0]), .in1(in_2[1]), .in0(in_2[0]),
    .n2(state_trans1_1_n0[2]), .n1(state_trans1_1_n0[1]), .n0(state_trans1_1_n0[0]));
  state_trans2 state_trans2_1 (
    .s2(register_2_q[2]), .s1(register_2_q[1]), .s0(register_2_q[0]), .in1(in_2[1]), .in0(in_2[0]),
    .n2(state_trans2_1_n0[2]), .n1(state_trans2_1_n0[1]), .n0(state_trans2_1_n0[0]));
  meely2 meely2_1 (
    .s2(register_2_q[2]), .s1(register_2_q[1]), .s0(register_2_q[0]), .in1(in_2[1]), .in0(in_2[0]),
    .o(meely2_1_o));
  or or_1 (out_3, meely1_1_o, meely2_1_o);
endmodule

module state_trans1 (
  input  s2,
  input  s1,
  input  s0,
  input  in1,
  input  in0,
  output n2,
  output n1,
  output n0
);

  wire and_1_out, and_2_out, and_3_out, and_4_out, and_5_out, and_6_out, and_7_out, and_8_out, not_1_out,
       not_2_out, not_3_out, not_4_out, not_5_out, not_6_out, not_7_out, not_8_out, not_9_out, not_10_out,
       not_11_out, not_12_out, not_13_out, not_14_out, not_15_out, not_16_out, not_17_out, not_18_out,
       not_19_out, not_20_out, not_21_out, not_22_out, not_23_out;

  not not_1 (not_1_out, s2);
  not not_2 (not_2_out, in1);
  not not_3 (not_3_out, in0);
  not not_4 (not_4_out, s1);
  not not_5 (not_5_out, s0);
  not not_6 (not_6_out, in0);
  not not_7 (not_7_out, s2);
  not not_8 (not_8_out, s1);
  not not_9 (not_9_out, in1);
  not not_10 (not_10_out, in0);
  not not_11 (not_11_out, s2);
  not not_12 (not_12_out, s0);
  not not_13 (not_13_out, in0);
  not not_14 (not_14_out, s2);
  not not_15 (not_15_out, in1);
  not not_16 (not_16_out, s1);
  not not_17 (not_17_out, in1);
  not not_18 (not_18_out, s2);
  not not_19 (not_19_out, s0);
  not not_20 (not_20_out, in0);
  not not_21 (not_21_out, s1);
  not not_22 (not_22_out, s0);
  not not_23 (not_23_out, in0);
  and and_1 (and_1_out, not_1_out, s1, s0, not_2_out, not_3_out);
  and and_2 (and_2_out, s2, not_4_out, not_5_out, in1, not_6_out);
  and and_3 (and_3_out, not_7_out, not_8_out, s0, not_9_out, not_10_out);
  and and_4 (and_4_out, not_11_out, s1, not_12_out, in1, not_13_out);
  and and_5 (and_5_out, not_14_out, not_15_out, in0);
  and and_6 (and_6_out, not_16_out, not_17_out, in0);
  and and_7 (and_7_out, not_18_out, s1, not_19_out, in1, not_20_out);
  and and_8 (and_8_out, s2, not_21_out, not_22_out, in1, not_23_out);
  or or_1 (n2, and_1_out, and_2_out);
  or or_2 (n1, and_3_out, and_4_out);
  or or_3 (n0, and_5_out, and_6_out, and_7_out, and_8_out);
endmodule

module state_trans2 (
  input  s2,
  input  s1,
  input  s0,
  input  in1,
  input  in0,
  output n2,
  output n1,
  output n0
);

  wire and_1_out, and_2_out, and_3_out, and_4_out, and_5_out, and_6_out, and_7_out, and_8_out, and_9_out,
       and_10_out, and_11_out, not_1_out, not_2_out, not_3_out, not_4_out, not_5_out, not_6_out, not_7_out,
       not_8_out, not_9_out, not_10_out, not_11_out, not_12_out, not_13_out, not_14_out, not_15_out,
       not_16_out, not_17_out, not_18_out, not_19_out, not_20_out, not_21_out, not_22_out, not_23_out,
       not_24_out, not_25_out, not_26_out, not_27_out, not_28_out, not_29_out, not_30_out;

  not not_1 (not_1_out, s2);
  not not_2 (not_2_out, in0);
  not not_3 (not_3_out, s1);
  not not_4 (not_4_out, s0);
  not not_5 (not_5_out, in1);
  not not_6 (not_6_out, in0);
  not not_7 (not_7_out, s1);
  not not_8 (not_8_out, in0);
  not not_9 (not_9_out, s2);
  not not_10 (not_10_out, s1);
  not not_11 (not_11_out, in1);
  not not_12 (not_12_out, s2);
  not not_13 (not_13_out, s0);
  not not_14 (not_14_out, in1);
  not not_15 (not_15_out, s1);
  not not_16 (not_16_out, in0);
  not not_17 (not_17_out, s1);
  not not_18 (not_18_out, s0);
  not not_19 (not_19_out, in1);
  not not_20 (not_20_out, s2);
  not not_21 (not_21_out, s0);
  not not_22 (not_22_out, in1);
  not not_23 (not_23_out, in0);
  not not_24 (not_24_out, s2);
  not not_25 (not_25_out, in1);
  not not_26 (not_26_out, s1);
  not not_27 (not_27_out, s0);
  not not_28 (not_28_out, in1);
  not not_29 (not_29_out, s1);
  not not_30 (not_30_out, in1);
  and and_1 (and_1_out, not_1_out, s1, s0, in1, not_2_out);
  and and_2 (and_2_out, s2, not_3_out, not_4_out, not_5_out, not_6_out);
  and and_3 (and_3_out, s2, not_7_out, s0, in1, not_8_out);
  and and_4 (and_4_out, not_9_out, not_10_out, s0, not_11_out, in0);
  and and_5 (and_5_out, not_12_out, s1, not_13_out, not_14_out);
  and and_6 (and_6_out, s2, not_15_out, s0, in1, not_16_out);
  and and_7 (and_7_out, not_17_out, not_18_out, not_19_out, in0);
  and and_8 (and_8_out, not_20_out, s1, not_21_out, not_22_out, not_23_out);
  and and_9 (and_9_out, not_24_out, s1, s0, not_25_out, in0);
  and and_10 (and_10_out, s2, not_26_out, not_27_out, not_28_out);
  and and_11 (and_11_out, s2, not_29_out, not_30_out, in0);
  or or_1 (n2, and_1_out, and_2_out, and_3_out);
  or or_2 (n1, and_4_out, and_5_out, and_6_out);
  or or_3 (n0, and_7_out, and_8_out, and_9_out, and_10_out, and_11_out);
endmodule

module meely1 (
  input  s2,
  input  s1,
  input  s0,
  input  in1,
  input  in0,
  output o
);

  wire not_1_out, not_2_out, not_3_out;

  not not_1 (not_1_out, s1);
  not not_2 (not_2_out, s0);
  not not_3 (not_3_out, in0);
  and and_1 (o, s2, not_1_out, not_2_out, in1, not_3_out);
endmodule

module meely2 (
  input  s2,
  input  s1,
  input  s0,
  input  in1,
  input  in0,
  output o
);

  wire not_1_out, not_2_out;

  not not_1 (not_1_out, s1);
  not not_2 (not_2_out, in0);
  and and_1 (o, s2, not_1_out, s0, in1, not_2_out);
endmodule
