// Logisim project grf.circ as structural Verilog: 1 circuit, main circuit grf
module grf (
  input  reset,
  input  in_2,
  input  [4:0] RA1,
  input  [31:0] in_4,
  input  [4:0] RA2,
  input  [4:0] WA,
  input  write_enable,
  output [31:0] out_8,
  output [31:0] out_9
);

  wire [31:0] _1, _2, _3, _4, _5, _6, _7, _8, _9, _10, _11, _12, _13, _14, _15, _16, _17, _18, _19, _20, _21,
       _22, _23, _24, _25, _26, _27, _28, _29, _30, _31, _32, r1, r2, r3, r4, r5, r6, r7, r8, r9, r10, r11,
       r12, r13, r14, r15, r16, r17, r18, r19, r20, r21, r22, r23, r24, r25, r26, r27, r28, r29, r30, r31,
       r32;

  Register #(.width(32)) register_1 (.D({32{1'b0}}), .Q(r1), .clk(reset), .clr(in_2));  // open: en
  Register #(.width(32)) register_2 (.D(_9), .Q(r9), .clk(reset), .clr(in_2));  // open: en
  Register #(.width(32)) register_3 (.D(_17), .Q(r17), .clk(reset), .clr(in_2));  // open: en
  Register #(.width(32)) register_4 (.D(_25), .Q(r25), .clk(reset), .clr(in_2));  // open: en
  Multiplexer #(.select(5), .width(32)) multiplexer_1 (
    .in0(r1), .in1(r2), .in2(r3), .in3(r4), .in4(r5), .in5(r6), .in6(r7), .in7(r8), .in8(r9), .in9(r10),
    .in10(r11), .in11(r12), .in12(r13), .in13(r14), .in14(r15), .in15(r16), .in16(r17), .in17(r18),
    .in18(r19), .in19(r20), .in20(r21), .in21(r22), .in22(r23), .in23(r24), .in24(r25), .in25(r26),
    .in26(r27), .in27(r28), .in28(r29), .in29(r30), .in30(r31), .in31(r32), .out(out_8), .sel(RA1));  // open: en
  Register #(.width(32)) register_5 (.D(_2), .Q(r2), .clk(reset), .clr(in_2));  // open: en
  Register #(.width(32)) register_6 (.D(_10), .Q(r10), .clk(reset), .clr(in_2));  // open: en
  Register #(.width(32)) register_7 (.D(_18), .Q(r18), .clk(reset), .clr(in_2));  // open: en
  Register #(.width(32)) register_8 (.D(_26), .Q(r26), .clk(reset), .clr(in_2));  // open: en
  Register #(.width(32)) register_9 (.D(_3), .Q(r3), .clk(reset), .clr(in_2));  // open: en
  Register #(.width(32)) register_10 (.D(_11), .Q(r11), .clk(reset), .clr(in_2));  // open: en
  Register #(.width(32)) register_11 (.D(_19), .Q(r19), .clk(reset), .clr(in_2));  // open: en
  Register #(.width(32)) register_12 (.D(_27), .Q(r27), .clk(reset), .clr(in_2));  // open: en
  Register #(.width(32)) register_13 (.D(_4), .Q(r4), .clk(reset), .clr(in_2));  // open: en
  Register #(.width(32)) register_14 (.D(_12), .Q(r12), .clk(reset), .clr(in_2));  // open: en
  Register #(.width(32)) register_15 (.D(_20), .Q(r20), .clk(reset), .clr(in_2));  // open: en
  Register #(.width(32)) register_16 (.D(_28), .Q(r28), .clk(reset), .clr(in_2));  // open: en
  Register #(.width(32)) register_17 (.D(_5), .Q(r5), .clk(reset), .clr(in_2));  // open: en
  Register #(.width(32)) register_18 (.D(_13), .Q(r13), .clk(reset), .clr(in_2));  // open: en
  Register #(.width(32)) register_19 (.D(_21), .Q(r21), .clk(reset), .clr(in_2));  // open: en
  Register #(.width(32)) register_20 (.D(_29), .Q(r29), .clk(reset), .clr(in_2));  // open: en
  Register #(.width(32)) register_21 (.D(_6), .Q(r6), .clk(reset), .clr(in_2));  // open: en
  Register #(.width(32)) register_22 (.D(_14), .Q(r14), .clk(reset), .clr(in_2));  // open: en
  Register #(.width(32)) register_23 (.D(_22), .Q(r22), .clk(reset), .clr(in_2));  // open: en
  Register #(.width(32)) register_24 (.D(_30), .Q(r30), .clk(reset), .clr(in_2));  // open: en
  Register #(.width(32)) register_25 (.D(_7), .Q(r7), .clk(reset), .clr(in_2));  // open: en
  Register #(.width(32)) register_26 (.D(_15), .Q(r15), .clk(reset), .clr(in_2));  // open: en
  Register #(.width(32)) register_27 (.D(_23), .Q(r23), .clk(reset), .clr(in_2));  // open: en
  Register #(.width(32)) register_28 (.D(_31), .Q(r31), .clk(reset), .clr(in_2));  // open: en
  Register #(.width(32)) register_29 (.D(_8), .Q(r8), .clk(reset), .clr(in_2));  // open: en
  Register #(.width(32)) register_30 (.D(_16), .Q(r16), .clk(reset), .clr(in_2));  // open: en
  Register #(.width(32)) register_31 (.D(_24), .Q(r24), .clk(reset), .clr(in_2));  // open: en
  Register #(.width(32)) register_32 (.D(_32), .Q(r32), .clk(reset), .clr(in_2));  // open: en
  Multiplexer #(.select(5), .width(32)) multiplexer_2 (
    .in0(r1), .in1(r2), .in2(r3), .in3(r4), .in4(r5), .in5(r6), .in6(r7), .in7(r8), .in8(r9), .in9(r10),
    .in10(r11), .in11(r12), .in12(r13), .in13(r14), .in14(r15), .in15(r16), .in16(r17), .in17(r18),
    .in18(r19), .in19(r20), .in20(r21), .in21(r22), .in22(r23), .in23(r24), .in24(r25), .in25(r26),
    .in26(r27), .in27(r28), .in28(r29), .in29(r30), .in30(r31), .in31(r32), .out(out_9), .sel(RA2));  // open: en
  Demultiplexer #(.select(5), .width(32), .tristate("true")) demultiplexer_1 (
    .out0(_1), .out1(_2), .out2(_3), .out3(_4), .out4(_5), .out5(_6), .out6(_7), .out7(_8), .out8(_9),
    .out9(_10), .out10(_11), .out11(_12), .out12(_13), .out13(_14), .out14(_15), .out15(_16), .out16(_17),
    .out17(_18), .out18(_19), .out19(_20), .out20(_21), .out21(_22), .out22(_23), .out23(_24), .out24(_25),
    .out25(_26), .out26(_27), .out27(_28), .out28(_29), .out29(_30), .out30(_31), .out31(_32), .in(in_4),
    .sel(WA), .en(write_enable));

  // Notes on the sheet:
  //   clk
  //   RD1
  //   RD2
  //   WD
endmodule
