// Logisim project grf_wu.circ as structural Verilog: 1 circuit, main circuit grf
module grf (
  input  clk,
  input  reset,
  input  WE,
  input  [4:0] A1,
  input  [4:0] A2,
  input  [4:0] A3,
  input  [31:0] in_7,
  output [31:0] out_8,
  output [31:0] out_9
);

  wire in00, in01, in02, in03, in04, in05, in06, in07, in08, in09, in10, in11, in12, in13, in14, in15, in16,
       in17, in18, in19, in20, in21, in22, in23, in24, in25, in26, in27, in28, in29, in30, in31;
  wire [31:0] out00, out01, out02, out03, out04, out05, out06, out07, out08, out09, out10, out11, out12,
       out13, out14, out15, out16, out17, out18, out19, out20, out21, out22, out23, out24, out25, out26,
       out27, out28, out29, out30, out31;

  Register #(.width(32)) register_1 (.D({32{1'b0}}), .en(in00), .Q(out00), .clk(clk), .clr(reset));
  Register #(.width(32)) register_2 (.D(in_7), .en(in08), .Q(out08), .clk(clk), .clr(reset));
  Register #(.width(32)) register_3 (.D(in_7), .en(in16), .Q(out16), .clk(clk), .clr(reset));
  Register #(.width(32)) register_4 (.D(in_7), .en(in24), .Q(out24), .clk(clk), .clr(reset));
  Demultiplexer #(.select(5), .disabled(0), .enable("false")) demultiplexer_1 (
    .out0(in00), .out1(in01), .out2(in02), .out3(in03), .out4(in04), .out5(in05), .out6(in06), .out7(in07),
    .out8(in08), .out9(in09), .out10(in10), .out11(in11), .out12(in12), .out13(in13), .out14(in14),
    .out15(in15), .out16(in16), .out17(in17), .out18(in18), .out19(in19), .out20(in20), .out21(in21),
    .out22(in22), .out23(in23), .out24(in24), .out25(in25), .out26(in26), .out27(in27), .out28(in28),
    .out29(in29), .out30(in30), .out31(in31), .in(WE), .sel(A3));
  Register #(.width(32)) register_5 (.D(in_7), .en(in01), .Q(out01), .clk(clk), .clr(reset));
  Register #(.width(32)) register_6 (.D(in_7), .en(in09), .Q(out09), .clk(clk), .clr(reset));
  Register #(.width(32)) register_7 (.D(in_7), .en(in17), .Q(out17), .clk(clk), .clr(reset));
  Register #(.width(32)) register_8 (.D(in_7), .en(in25), .Q(out25), .clk(clk), .clr(reset));
  Register #(.width(32)) register_9 (.D(in_7), .en(in02), .Q(out02), .clk(clk), .clr(reset));
  Register #(.width(32)) register_10 (.D(in_7), .en(in10), .Q(out10), .clk(clk), .clr(reset));
  Register #(.width(32)) register_11 (.D(in_7), .en(in18), .Q(out18), .clk(clk), .clr(reset));
  Register #(.width(32)) register_12 (.D(in_7), .en(in26), .Q(out26), .clk(clk), .clr(reset));
  Register #(.width(32)) register_13 (.D(in_7), .en(in03), .Q(out03), .clk(clk), .clr(reset));
  Register #(.width(32)) register_14 (.D(in_7), .en(in11), .Q(out11), .clk(clk), .clr(reset));
  Register #(.width(32)) register_15 (.D(in_7), .en(in19), .Q(out19), .clk(clk), .clr(reset));
  Register #(.width(32)) register_16 (.D(in_7), .en(in27), .Q(out27), .clk(clk), .clr(reset));
  Multiplexer #(.select(5), .width(32), .enable("false")) multiplexer_1 (
    .in0(out00), .in1(out01), .in2(out02), .in3(out03), .in4(out04), .in5(out05), .in6(out06), .in7(out07),
    .in8(out08), .in9(out09), .in10(out10), .in11(out11), .in12(out12), .in13(out13), .in14(out14),
    .in15(out15), .in16(out16), .in17(out17), .in18(out18), .in19(out19), .in20(out20), .in21(out21),
    .in22(out22), .in23(out23), .in24(out24), .in25(out25), .in26(out26), .in27(out27), .in28(out28),
    .in29(out29), .in30(out30), .in31(out31), .out(out_8), .sel(A1));
  Register #(.width(32)) register_17 (.D(in_7), .en(in04), .Q(out04), .clk(clk), .clr(reset));
  Register #(.width(32)) register_18 (.D(in_7), .en(in12), .Q(out12), .clk(clk), .clr(reset));
  Register #(.width(32)) register_19 (.D(in_7), .en(in20), .Q(out20), .clk(clk), .clr(reset));
  Register #(.width(32)) register_20 (.D(in_7), .en(in28), .Q(out28), .clk(clk), .clr(reset));
  Register #(.width(32)) register_21 (.D(in_7), .en(in05), .Q(out05), .clk(clk), .clr(reset));
  Register #(.width(32)) register_22 (.D(in_7), .en(in13), .Q(out13), .clk(clk), .clr(reset));
  Register #(.width(32)) register_23 (.D(in_7), .en(in21), .Q(out21), .clk(clk), .clr(reset));
  Register #(.width(32)) register_24 (.D(in_7), .en(in29), .Q(out29), .clk(clk), .clr(reset));
  Multiplexer #(.select(5), .width(32), .enable("false")) multiplexer_2 (
    .in0(out00), .in1(out01), .in2(out02), .in3(out03), .in4(out04), .in5(out05), .in6(out06), .in7(out07),
    .in8(out08), .in9(out09), .in10(out10), .in11(out11), .in12(out12), .in13(out13), .in14(out14),
    .in15(out15), .in16(out16), .in17(out17), .in18(out18), .in19(out19), .in20(out20), .in21(out21),
    .in22(out22), .in23(out23), .in24(out24), .in25(out25), .in26(out26), .in27(out27), .in28(out28),
    .in29(out29), .in30(out30), .in31(out31), .out(out_9), .sel(A2));
  Register #(.width(32)) register_25 (.D(in_7), .en(in06), .Q(out06), .clk(clk), .clr(reset));
  Register #(.width(32)) register_26 (.D(in_7), .en(in14), .Q(out14), .clk(clk), .clr(reset));
  Register #(.width(32)) register_27 (.D(in_7), .en(in22), .Q(out22), .clk(clk), .clr(reset));
  Register #(.width(32)) register_28 (.D(in_7), .en(in30), .Q(out30), .clk(clk), .clr(reset));
  Register #(.width(32)) register_29 (.D(in_7), .en(in07), .Q(out07), .clk(clk), .clr(reset));
  Register #(.width(32)) register_30 (.D(in_7), .en(in15), .Q(out15), .clk(clk), .clr(reset));
  Register #(.width(32)) register_31 (.D(in_7), .en(in23), .Q(out23), .clk(clk), .clr(reset));
  Register #(.width(32)) register_32 (.D(in_7), .en(in31), .Q(out31), .clk(clk), .clr(reset));

  // Other names for the same wires on the sheet: RD1[31:0] = out_8; RD2[31:0] = out_9; WD[31:0] = in_7
endmodule
