// Logisim project my_first_cpu - 副本.circ as structural Verilog: 9 circuits, main circuit main
module main (
  input  in_1,
  output [31:0] out_2,
  output out_3,
  output [4:0] out_4,
  output [31:0] out_5,
  output out_6,
  output [4:0] out_7,
  output [31:0] out_8
);

  wire ALUSrc, Branch, clk, j_jal_imm, jal, jr, not_1_out, Sign, zero;
  wire [1:0] RegDst, WhReg;
  wire [3:0] ALUOp;
  wire [4:0] _15_11, cyw_sp_splitter_1__20_16, cyw_sp_splitter_1__25_21, shamt;
  wire [5:0] cyw_sp_splitter_1__5_0, cyw_sp_splitter_1__31_26;
  wire [15:0] cyw_sp_splitter_1__15_0;
  wire [25:0] jaddr;
  wire [31:0] alu_1_out_5, and_1_out, bit_extender_1_out, bit_extender_2_out, bit_extender_3_out,
       data_mem_1_readdata, grf_1_out_8, multiplexer_1_out, multiplexer_3_out, npc_1_out_9, PC_4, PC_q,
       shifter_1_out;

  assign and_1_out = npc_1_out_9 & 32'h7f;  // AND_Gate and_1, 32 bits wide
  Clock clock_1 (.out(clk));
  // Probe on PC_q
  Register #(.width(32)) PC (.D(and_1_out), .en(not_1_out), .Q(PC_q), .clk(clk), .clr(in_1));
  not not_1 (not_1_out, 1'b0);
  Adder #(.width(32)) adder_1 (.a(32'h4), .b(PC_q), .out(PC_4));  // open: cin, cout
  instr_mem instr_mem_1 (.in_1(PC_q), .out_2(out_2));
  NPC npc_1 (
    .Branch(Branch), .Jump(j_jal_imm), .ALUzero(zero), .in_5(PC_q), .in_6(jaddr), .in_7(bit_extender_2_out),
    .out_9(npc_1_out_9), .in_8(grf_1_out_8), .Jr(jr));
  cyw_sp_splitter cyw_sp_splitter_1 (
    .in_1(out_2), ._5_0(cyw_sp_splitter_1__5_0), ._10_6(shamt), ._15_11(_15_11),
    ._20_16(cyw_sp_splitter_1__20_16), ._25_21(cyw_sp_splitter_1__25_21), ._31_26(cyw_sp_splitter_1__31_26),
    .out_8(jaddr), ._15_0(cyw_sp_splitter_1__15_0));
  assign bit_extender_1_out = {{16{1'b0}}, cyw_sp_splitter_1__15_0};  // Bit_Extender bit_extender_1
  assign bit_extender_2_out = {{16{cyw_sp_splitter_1__15_0[15]}}, cyw_sp_splitter_1__15_0};  // Bit_Extender bit_extender_2
  // Probe on cyw_sp_splitter_1__15_0
  control control_1 (
    .opcode(cyw_sp_splitter_1__31_26), .func(cyw_sp_splitter_1__5_0), .RegWrite(out_3), .RegDst(RegDst),
    .ALUSrc(ALUSrc), .Branch(Branch), .MemWrite(out_6), .WhichtoReg(WhReg), .jr(jr), .j_jal_imm(j_jal_imm),
    .jal__31(jal), .ALUOp(ALUOp), .sign(Sign));
  assign bit_extender_3_out = {{16{1'b0}}, cyw_sp_splitter_1__15_0};  // Bit_Extender bit_extender_3
  Multiplexer #(.width(32)) multiplexer_1 (
    .in0(bit_extender_1_out), .in1(bit_extender_2_out), .out(multiplexer_1_out), .sel(Sign));  // open: en
  // Probe on out_4
  // Probe on out_5
  Multiplexer #(.select(2), .width(5)) multiplexer_2 (
    .in0(cyw_sp_splitter_1__20_16), .in1(_15_11), .in2({5{1'b1}}), .out(out_4), .sel(RegDst));  // open: in3, en
  Shifter #(.width(32)) shifter_1 (.in(bit_extender_3_out), .\dist (5'b10000), .out(shifter_1_out));
  // Probe on out_2
  grf grf_1 (
    .reset(clk), .in_2(in_1), .RA1(cyw_sp_splitter_1__25_21), .RA2(cyw_sp_splitter_1__20_16), .WA(out_4),
    .write_enable(out_3), .in_4(out_5), .out_8(grf_1_out_8), .out_9(out_8));
  Multiplexer #(.width(32)) multiplexer_3 (
    .in0(out_8), .in1(multiplexer_1_out), .out(multiplexer_3_out), .sel(ALUSrc));  // open: en
  ALU alu_1 (
    .srcA(grf_1_out_8), .srcB(multiplexer_3_out), .in_3(ALUOp), .in_4(shamt), .out_7(zero),
    .out_5(alu_1_out_5));  // open: overflow
  data_mem data_mem_1 (
    .A(alu_1_out_5), .WD(out_8), .ReadData(data_mem_1_readdata), .in_1(clk), .MemWrite(out_6), .out_5(out_7));
  Multiplexer #(.select(2), .width(32)) multiplexer_4 (
    .in0(alu_1_out_5), .in1(data_mem_1_readdata), .in2(shifter_1_out), .in3(PC_4), .out(out_5), .sel(WhReg));  // open: en
  // Probe on nothing

  // Other names for the same wires on the sheet: Instr[31:0] = out_2; MemAddr[4:0] = out_7; MemData[31:0] = out_8;
  //   MemWrite = out_6; RegAddr[4:0] = out_4; RegData[31:0] = out_5; RegWrite = out_3; reset = in_1

  // Notes on the sheet:
  //   halt
  //   lw $v0, 4($t)/label($t)->imm=1
  //   lw/sw/beq offset(sign_ext)
  //   andi/ori zero_ext
  //   Itype_Dst
  //   Jtype_Dst
  //   I type rt对应着寄存
  //   A3_sel
  //   下次试试把lui的imm放到alu里试试
  //   PC <- R[rs], Rtype
  //   lui lane
  //   jal lane
  //   WD_sel
endmodule

module instr_mem (
  input  [31:0] in_1,
  output [31:0] out_2
);

  wire [31:0] addr_proccess_1_out_2;

  addr_proccess addr_proccess_1 (.in_1(in_1), .out_2(addr_proccess_1_out_2));
  ROM #(.addrWidth(5), .dataWidth(32)) rom_1 (.addr(addr_proccess_1_out_2[6:2]), .data(out_2));  // open: sel

  // Notes on the sheet:
  //   PC
  //   contents of rom_1 (hex, n*v repeats v):
  //   34490064 344a00fa 344b00c8 12b6021 18a6823 ac4d0004 8c4e0004 3c0f0064 11a9fffe 11cdfffd
  //   mem[PC]
  //   mips定位到byte, 所以一般xxx00
  //   logisimyi以4byte为一个单位, 所以一般xxx
endmodule

module cyw_sp_splitter (
  input  [31:0] in_1,
  output [5:0] _5_0,
  output [4:0] _10_6,
  output [4:0] _15_11,
  output [4:0] _20_16,
  output [4:0] _25_21,
  output [5:0] _31_26,
  output [25:0] out_8,
  output [15:0] _15_0
);


  assign _5_0 = in_1[5:0];
  assign _10_6 = in_1[10:6];
  assign _15_0 = in_1[15:0];
  assign _15_11 = in_1[15:11];
  assign _20_16 = in_1[20:16];
  assign _25_21 = in_1[25:21];
  assign _31_26 = in_1[31:26];
  assign out_8 = in_1[25:0];

  // Notes on the sheet:
  //   [26:0]
  //   J/R
endmodule

module grf (
  input  reset,
  input  in_2,
  input  [4:0] RA1,
  input  [31:0] in_4,
  input  [4:0] RA2,
  input  [4:0] WA,
  input  write_enable,
  output [31:0] out_8,
  output [31:0] out_9
);

  wire [31:0] _0, _1, _2, _3, _4, _5, _6, _7, _8, _9, _10, _11, _12, _13, _14, _15, _16, _17, _18, _19, _20,
       _21, _22, _23, _24, _25, _26, _27, _28, _29, _30, _31, r0, r1, r2, r3, r4, r5, r6, r7, r8, r9, r10,
       r11, r12, r13, r14, r15, r16, r17, r18, r19, r20, r21, r22, r23, r24, r25, r26, r27, r28, r29, r30,
       r31;

  Register #(.width(32)) register_1 (.D({32{1'b0}}), .Q(r0), .clk(reset), .clr(in_2));  // open: en
  Register #(.width(32)) register_2 (.D(_8), .Q(r8), .clk(reset), .clr(in_2));  // open: en
  Register #(.width(32)) register_3 (.D(_16), .Q(r16), .clk(reset), .clr(in_2));  // open: en
  Register #(.width(32)) register_4 (.D(_24), .Q(r24), .clk(reset), .clr(in_2));  // open: en
  Multiplexer #(.select(5), .width(32)) multiplexer_1 (
    .in0(r0), .in1(r1), .in2(r2), .in3(r3), .in4(r4), .in5(r5), .in6(r6), .in7(r7), .in8(r8), .in9(r9),
    .in10(r10), .in11(r11), .in12(r12), .in13(r13), .in14(r14), .in15(r15), .in16(r16), .in17(r17),
    .in18(r18), .in19(r19), .in20(r20), .in21(r21), .in22(r22), .in23(r23), .in24(r24), .in25(r25),
    .in26(r26), .in27(r27), .in28(r28), .in29(r29), .in30(r30), .in31(r31), .out(out_8), .sel(RA1));  // open: en
  Register #(.width(32)) register_5 (.D(_1), .Q(r1), .clk(reset), .clr(in_2));  // open: en
  Register #(.width(32)) register_6 (.D(_9), .Q(r9), .clk(reset), .clr(in_2));  // open: en
  Register #(.width(32)) register_7 (.D(_17), .Q(r17), .clk(reset), .clr(in_2));  // open: en
  Register #(.width(32)) register_8 (.D(_25), .Q(r25), .clk(reset), .clr(in_2));  // open: en
  Register #(.width(32)) register_9 (.D(_2), .Q(r2), .clk(reset), .clr(in_2));  // open: en
  Register #(.width(32)) register_10 (.D(_10), .Q(r10), .clk(reset), .clr(in_2));  // open: en
  Register #(.width(32)) register_11 (.D(_18), .Q(r18), .clk(reset), .clr(in_2));  // open: en
  Register #(.width(32)) register_12 (.D(_26), .Q(r26), .clk(reset), .clr(in_2));  // open: en
  Register #(.width(32)) register_13 (.D(_3), .Q(r3), .clk(reset), .clr(in_2));  // open: en
  Register #(.width(32)) register_14 (.D(_11), .Q(r11), .clk(reset), .clr(in_2));  // open: en
  Register #(.width(32)) register_15 (.D(_19), .Q(r19), .clk(reset), .clr(in_2));  // open: en
  Register #(.width(32)) register_16 (.D(_27), .Q(r27), .clk(reset), .clr(in_2));  // open: en
  Register #(.width(32)) register_17 (.D(_4), .Q(r4), .clk(reset), .clr(in_2));  // open: en
  Register #(.width(32)) register_18 (.D(_12), .Q(r12), .clk(reset), .clr(in_2));  // open: en
  Register #(.width(32)) register_19 (.D(_20), .Q(r20), .clk(reset), .clr(in_2));  // open: en
  Register #(.width(32)) register_20 (.D(_28), .Q(r28), .clk(reset), .clr(in_2));  // open: en
  Register #(.width(32)) register_21 (.D(_5), .Q(r5), .clk(reset), .clr(in_2));  // open: en
  Register #(.width(32)) register_22 (.D(_13), .Q(r13), .clk(reset), .clr(in_2));  // open: en
  Register #(.width(32)) register_23 (.D(_21), .Q(r21), .clk(reset), .clr(in_2));  // open: en
  Register #(.width(32)) register_24 (.D(_29), .Q(r29), .clk(reset), .clr(in_2));  // open: en
  Register #(.width(32)) register_25 (.D(_6), .Q(r6), .clk(reset), .clr(in_2));  // open: en
  Register #(.width(32)) register_26 (.D(_14), .Q(r14), .clk(reset), .clr(in_2));  // open: en
  Register #(.width(32)) register_27 (.D(_22), .Q(r22), .clk(reset), .clr(in_2));  // open: en
  Register #(.width(32)) register_28 (.D(_30), .Q(r30), .clk(reset), .clr(in_2));  // open: en
  Register #(.width(32)) register_29 (.D(_7), .Q(r7), .clk(reset), .clr(in_2));  // open: en
  Register #(.width(32)) register_30 (.D(_15), .Q(r15), .clk(reset), .clr(in_2));  // open: en
  Register #(.width(32)) register_31 (.D(_23), .Q(r23), .clk(reset), .clr(in_2));  // open: en
  Register #(.width(32)) register_32 (.D(_31), .Q(r31), .clk(reset), .clr(in_2));  // open: en
  Multiplexer #(.select(5), .width(32)) multiplexer_2 (
    .in0(r0), .in1(r1), .in2(r2), .in3(r3), .in4(r4), .in5(r5), .in6(r6), .in7(r7), .in8(r8), .in9(r9),
    .in10(r10), .in11(r11), .in12(r12), .in13(r13), .in14(r14), .in15(r15), .in16(r16), .in17(r17),
    .in18(r18), .in19(r19), .in20(r20), .in21(r21), .in22(r22), .in23(r23), .in24(r24), .in25(r25),
    .in26(r26), .in27(r27), .in28(r28), .in29(r29), .in30(r30), .in31(r31), .out(out_9), .sel(RA2));  // open: en
  Demultiplexer #(.select(5), .width(32), .tristate("true")) demultiplexer_1 (
    .out0(_0), .out1(_1), .out2(_2), .out3(_3), .out4(_4), .out5(_5), .out6(_6), .out7(_7), .out8(_8),
    .out9(_9), .out10(_10), .out11(_11), .out12(_12), .out13(_13), .out14(_14), .out15(_15), .out16(_16),
    .out17(_17), .out18(_18), .out19(_19), .out20(_20), .out21(_21), .out22(_22), .out23(_23), .out24(_24),
    .out25(_25), .out26(_26), .out27(_27), .out28(_28), .out29(_29), .out30(_30), .out31(_31), .in(in_4),
    .sel(WA), .en(write_enable));

  // Notes on the sheet:
  //   clk
  //   z
  //   t0
  //   s0
  //   t8
  //   at
  //   v0
  //   t9
  //   k0
  //   RD1
  //   v1
  //   k1
  //   a0
  //   gp
  //   sp
  //   fp
  //   a3
  //   t7
  //   s7
  //   ra
  //   RD2
  //   WD
endmodule

module ALU (
  input  [31:0] srcA,
  input  [31:0] srcB,
  input  [3:0] in_3,
  input  [4:0] in_4,
  output [31:0] out_5,
  output overflow,
  output out_7
);

  wire adder_1_cout, comparator_1_lt, subtractor_1_bout;
  wire [31:0] add, \and , \or , shift, slt, sub;

  Adder #(.width(32)) adder_1 (.a(srcA), .b(srcB), .out(add), .cout(adder_1_cout));  // open: cin
  Subtractor #(.width(32)) subtractor_1 (.a(srcA), .b(srcB), .out(sub), .bout(subtractor_1_bout));  // open: bin
  assign \and  = srcA & srcB;  // AND_Gate and_1, 32 bits wide
  assign \or  = srcA | srcB;  // OR_Gate or_1, 32 bits wide
  Shifter #(.width(32)) shifter_1 (.in(srcB), .\dist (in_4), .out(shift));
  Comparator #(.width(32)) comparator_1 (.a(srcA), .b(srcB), .eq(out_7), .lt(comparator_1_lt));  // open: gt
  assign slt = {{31{1'b0}}, comparator_1_lt};  // Bit_Extender bit_extender_1
  Multiplexer #(.select(4), .width(32)) multiplexer_1 (
    .in0(add), .in1(sub), .in2(\and ), .in3(\or ), .in4(shift), .in5(slt), .out(out_5), .sel(in_3));  // open: in6, in7, in8, in9, in10, in11, in12, in13, in14, in15, en
  or or_2 (overflow, adder_1_cout, subtractor_1_bout);

  // Other names for the same wires on the sheet: ALUcontrol[3:0] = in_3; shamt[4:0] = in_4

  // Notes on the sheet:
  //   set_rules
  //   + 0000
  //   - 0001
  //   & 0010
  //   | 0011
  //   << 0100
  //   slt 0101
endmodule

module data_mem (
  input  in_1,
  input  MemWrite,
  input  [31:0] A,
  input  [31:0] WD,
  output [4:0] out_5,
  output [31:0] ReadData
);

  wire [31:0] addr_proccess_1_out_2;

  addr_proccess addr_proccess_1 (.in_1(A), .out_2({addr_proccess_1_out_2[31:7], out_5, addr_proccess_1_out_2[1:0]}));
  RAM #(.addrWidth(5), .dataWidth(32), .bus("separate")) ram_1 (
    .addr(out_5), .din(WD), .data(ReadData), .str(MemWrite), .clk(in_1));  // open: sel, ld, clr
endmodule

module NPC (
  input  Branch,
  input  Jump,
  input  Jr,
  input  ALUzero,
  input  [31:0] in_5,
  input  [25:0] in_6,
  input  [31:0] in_7,
  input  [31:0] in_8,
  output [31:0] out_9
);

  wire and_1_out;
  wire [27:0] PC_4;
  wire [31:0] adder_2_out, imm_00, multiplexer_1_out, multiplexer_2_out;
  wire [31:28] jaddr_00;

  // Probe on in_5
  // Probe on in_6
  // Probe on in_7
  // Probe on in_8
  Adder #(.width(32)) adder_1 (.a(in_5), .b(32'h4), .out({jaddr_00, PC_4}));  // open: cin, cout
  Adder #(.width(32)) adder_2 (.a({jaddr_00, PC_4}), .b(imm_00), .out(adder_2_out));  // open: cin, cout
  Shifter #(.width(32)) shifter_1 (.in(in_7), .\dist (5'b00010), .out(imm_00));
  Multiplexer #(.width(32)) multiplexer_1 (
    .in0({jaddr_00, PC_4}), .in1(adder_2_out), .out(multiplexer_1_out), .sel(and_1_out));  // open: en
  and and_1 (and_1_out, Branch, ALUzero);
  Multiplexer #(.width(32)) multiplexer_2 (
    .in0(multiplexer_1_out), .in1({jaddr_00, in_6, 2'b00}), .out(multiplexer_2_out), .sel(Jump));  // open: en
  Multiplexer #(.width(32)) multiplexer_3 (.in0(multiplexer_2_out), .in1(in_8), .out(out_9), .sel(Jr));  // open: en
  // Probe on nothing

  // Other names for the same wires on the sheet: b = Branch; imm[31:0] = in_7; j = Jump; jaddr[25:0] = in_6;
  //   jaddr_00[27:2] = in_6; PC_4[31:28] = jaddr_00; PC[31:0] = in_5; regaddr[31:0] = in_8; zero = ALUzero

  // Notes on the sheet:
  //   next_PC
  //   PC+4
  //   PCbranch
  //   j
  //   regaddr
  //   (j/jal)
  //   imm26
  //   ext_imm16
endmodule

// controler
module control (
  input  [5:0] opcode,
  input  [5:0] func,
  output RegWrite,
  output [1:0] RegDst,
  output ALUSrc,
  output Branch,
  output MemWrite,
  output [1:0] WhichtoReg,
  output jr,
  output j_jal_imm,
  output jal__31,
  output [3:0] ALUOp,
  output sign
);

  wire add, addi, addiu, addu, \and , blez, j, lui, lw, not_1_out, not_2_out, not_3_out, not_4_out,
       not_5_out, not_6_out, not_7_out, not_8_out, not_9_out, not_10_out, not_11_out, not_12_out, \or , ori,
       Rtype, sll, sllv, slt, slti, sub, subu;

  not not_1 (not_1_out, opcode[5]);
  not not_2 (not_2_out, opcode[4]);
  not not_3 (not_3_out, opcode[3]);
  not not_4 (not_4_out, opcode[2]);
  not not_5 (not_5_out, opcode[1]);
  not not_6 (not_6_out, opcode[0]);
  and and_1 (Rtype, not_1_out, not_2_out, not_3_out, not_4_out, not_5_out, not_6_out);
  and and_2 (j, not_1_out, not_2_out, not_3_out, not_4_out, opcode[1], not_6_out);
  and and_3 (jal__31, not_1_out, not_2_out, not_3_out, not_4_out, opcode[1], opcode[0]);
  and and_4 (addi, not_1_out, not_2_out, opcode[3], not_4_out, not_5_out, not_6_out);
  and and_5 (ori, not_1_out, not_2_out, opcode[3], opcode[2], not_5_out, opcode[0]);
  and and_6 (lui, not_1_out, not_2_out, opcode[3], opcode[2], opcode[1], opcode[0]);
  and and_7 (slti, not_1_out, not_2_out, opcode[3], not_4_out, opcode[1], not_6_out);
  and and_8 (Branch, not_1_out, not_2_out, not_3_out, opcode[2], not_5_out, not_6_out);
  and and_9 (blez, not_1_out, not_2_out, not_3_out, opcode[2], opcode[1], not_6_out);
  and and_10 (MemWrite, opcode[5], not_2_out, opcode[3], not_4_out, opcode[1], opcode[0]);
  and and_11 (lw, opcode[5], not_2_out, not_3_out, not_4_out, opcode[1], opcode[0]);
  and and_12 (addiu, not_1_out, not_2_out, opcode[3], not_4_out, not_5_out, opcode[0]);
  and and_13 (jal__31, not_1_out, not_2_out, not_3_out, not_4_out, opcode[1], opcode[0]);
  not not_7 (not_7_out, func[4]);
  not not_8 (not_8_out, func[5]);
  not not_9 (not_9_out, func[2]);
  not not_10 (not_10_out, func[3]);
  not not_11 (not_11_out, func[1]);
  not not_12 (not_12_out, func[0]);
  and and_14 (add, Rtype, func[5], not_7_out, not_10_out, not_9_out, not_11_out, not_12_out);
  and and_15 (sub, Rtype, func[5], not_7_out, not_10_out, not_9_out, func[1], not_12_out);
  and and_16 (\and , Rtype, func[5], not_7_out, not_10_out, func[2], not_11_out, not_12_out);
  and and_17 (\or , Rtype, func[5], not_7_out, not_10_out, func[2], not_11_out, func[0]);
  and and_18 (sll, Rtype, not_8_out, not_7_out, not_10_out, not_9_out, not_11_out, not_12_out);
  and and_19 (sllv, Rtype, not_8_out, not_7_out, not_10_out, func[2], not_11_out, not_12_out);
  and and_20 (slt, Rtype, func[5], not_7_out, func[3], not_9_out, func[1], not_12_out);
  and and_21 (jr, Rtype, not_8_out, not_7_out, not_10_out, not_9_out, func[1], not_12_out);
  and and_22 (addu, Rtype, func[5], not_7_out, not_10_out, not_9_out, not_11_out, func[0]);
  and and_23 (subu, Rtype, func[5], not_7_out, not_10_out, not_9_out, func[1], func[0]);
  or or_1 (ALUOp[0], subu, \or , slti, sub, ori, slt);
  or or_2 (RegWrite, add, sub, \and , \or , sll, jal__31, sllv, addi, slt, ori, lw, lui, addiu, slti, addu, Branch, subu);
  or or_3 (RegDst[0], addu, subu, add, sll, sub, sllv, \and , slt, \or , jr);
  or or_4 (ALUSrc, addi, MemWrite, ori, lw, lui, addiu, slti);
  or or_5 (WhichtoReg[0], jal__31, lw);
  or or_6 (WhichtoReg[1], jal__31, lui);
  or or_7 (j_jal_imm, j, jal__31);
  or or_8 (ALUOp[1], \or , ori, \and );
  or or_9 (ALUOp[2], sllv, slt, slti, sll);
  or or_10 (sign, Branch, MemWrite, lw);

  assign ALUOp[3] = 1'b0;
  assign RegDst[1] = jal__31;

  // Other names for the same wires on the sheet: beq = Branch; jal = jal__31; sw = MemWrite

  // Notes on the sheet:
  //   j
  //   link
  //   00 AluRes->Reg
  //   01 Mem->Reg
  //   10 lui to Reg
  //   11 PC+4 -> Reg
endmodule

module addr_proccess (
  input  [31:0] in_1,
  output [31:0] out_2
);

  wire comparator_1_gt;
  wire [31:0] subtractor_1_out;

  // Probe on in_1
  Subtractor #(.width(32)) subtractor_1 (.a(in_1), .b(32'h3000), .out(subtractor_1_out));  // open: bin, bout
  Multiplexer #(.width(32)) multiplexer_1 (
    .in0(in_1), .in1(subtractor_1_out), .out(out_2), .sel(comparator_1_gt));  // open: en
  Comparator #(.width(32)) comparator_1 (.a(in_1), .b(32'h3000), .gt(comparator_1_gt));  // open: eq, lt
  // Probe on out_2
endmodule
